// Logisim project 16-bit_2-address-indirect addressing mode.circ as structural Verilog: 7 circuits, main circuit main
// R1
module main (
  input  [7:0] in_1,
  input  in_2,
  output [19:0] out_3,
  output ZERO,
  output CARRY,
  output SIGN,
  output ODD_PARITY,
  output EVEN_PARITY
);

  wire clock_1_out, nor_1_out, nor_2_out, not_1_out, shift_register_1_out, shift_register_2_out,
       shift_register_3_out;
  wire [3:0] demultiplexer_1_out0, demultiplexer_1_out1, multiplexer_1_out, Shifter_toalu;
  wire [7:0] MAR_q, programcounter_1_output, rom_2_data;
  wire [15:0] ALU_carry, LOAD_STORE_datamemory, LOAD_STORE_resister, multiplexer_2_out, multiplexer_3_out,
       multiplexer_4_out, R0_q, R1_q, R1_q_2, ram_1_data, RB_q, register_2_q, REGISTER_output32bit;
  wire [19:0] rom_1_data;
  wire [31:0] ALU_result;

  Clock clock_1 (.out(clock_1_out));
  Shift_Register #(.length(5)) shift_register_1 (
    .shift(in_2), .in(shift_register_1_out), .clk(clock_1_out), .out(shift_register_1_out));  // open: load, clr, d0, q0, d1, q1, d2, q2, d3, q3, d4, q4
  Register MAR (.D(programcounter_1_output), .Q(MAR_q), .clk(clock_1_out));  // open: en, clr
  PROGRAMCOUNTER programcounter_1 (
    .PC_IN(in_1), .CLOCK(clock_1_out), .PC_ENABLE(shift_register_2_out), .OUTPUT(programcounter_1_output));
  Shift_Register #(.length(5)) shift_register_2 (
    .shift(in_2), .in(shift_register_2_out), .clk(clock_1_out), .out(shift_register_2_out));  // open: load, clr, d0, q0, d1, q1, d2, q2, d3, q3, d4, q4
  nor nor_1 (nor_1_out, out_3[19], out_3[17], out_3[18]);
  Register #(.width(20)) MBR (.D(rom_1_data), .Q(out_3), .clk(clock_1_out));  // open: en, clr
  ROM #(.dataWidth(20)) rom_1 (.addr(MAR_q), .data(rom_1_data));  // open: sel
  Demultiplexer #(.width(4), .enable("false")) demultiplexer_1 (
    .out0(demultiplexer_1_out0), .out1(demultiplexer_1_out1), .in(out_3[19:16]), .sel(nor_1_out));
  Shift_Register #(.length(5)) shift_register_3 (
    .shift(in_2), .in(shift_register_3_out), .clk(clock_1_out), .out(shift_register_3_out));  // open: load, clr, d0, q0, d1, q1, d2, q2, d3, q3, d4, q4
  Multiplexer #(.width(4), .enable("false")) multiplexer_1 (
    .in0(out_3[11:8]), .in1(out_3[15:12]), .out(multiplexer_1_out), .sel(shift_register_3_out));
  Multiplexer #(.width(16), .enable("false")) multiplexer_2 (
    .in0(R1_q), .in1(LOAD_STORE_resister), .out(multiplexer_2_out), .sel(nor_1_out));
  register_file REGISTER (
    .INPUT(multiplexer_2_out), .CLOCK(clock_1_out), .READ_WRITE(shift_register_1_out),
    .SELECTBITS4BIT(multiplexer_1_out), .OUTPUT32BIT(REGISTER_output32bit));
  Register #(.width(16)) register_2 (.D(REGISTER_output32bit), .Q(register_2_q), .clk(clock_1_out));  // open: en, clr
  ROM rom_2 (.addr(out_3[7:0]), .data(rom_2_data));  // open: sel
  not not_1 (not_1_out, shift_register_1_out);
  load_store LOAD_STORE (
    .operand_resister(REGISTER_output32bit), .operand_datamemory(RB_q), .clock(clock_1_out),
    .opcode(demultiplexer_1_out1), .resister(LOAD_STORE_resister), .datamemory(LOAD_STORE_datamemory));
  Register #(.width(16)) R0 (.D(ALU_carry), .Q(R0_q), .clk(clock_1_out));  // open: en, clr
  alu ALU (
    ._32_bit_input_A(register_2_q), .inputB(RB_q), .shift_bit(Shifter_toalu), .carry(ALU_carry),
    .result(ALU_result), .opcode(demultiplexer_1_out0));
  Register #(.width(32)) R1 (.D(ALU_result), .Q({R1_q_2, R1_q}), .clk(clock_1_out));  // open: en, clr
  Multiplexer #(.width(16), .enable("false")) multiplexer_3 (
    .in0(RB_q), .in1(LOAD_STORE_datamemory), .out(multiplexer_3_out), .sel(nor_1_out));
  shifter Shifter (.inputfromRB(RB_q), .ToALU(Shifter_toalu));
  Register #(.width(16)) RB (.D(multiplexer_4_out), .Q(RB_q), .clk(clock_1_out));  // open: en, clr
  RAM #(.dataWidth(16), .bus("separate")) ram_1 (
    .addr(rom_2_data), .din(multiplexer_3_out), .data(ram_1_data), .str(not_1_out), .clk(clock_1_out),
    .ld(shift_register_1_out));  // open: sel, clr
  nor nor_2 (nor_2_out, R0_q[0], R0_q[1], R0_q[2], R0_q[3], R0_q[4], R0_q[5], R0_q[6], R0_q[7], R0_q[8], R0_q[9], R0_q[10], R0_q[11], R0_q[12], R0_q[13], R0_q[14], R0_q[15]);
  programStatusword PSW (
    .in_1(shift_register_3_out), .CLOCK(clock_1_out), .ZERO(ZERO), .CARRY(CARRY), .SIGN(SIGN),
    .ODD_PARITY(ODD_PARITY), .RESULTinput({R1_q_2, R1_q}), .CARRYinput(ALU_carry), .EVEN_PARITY(EVEN_PARITY));
  Multiplexer #(.width(16), .enable("false")) multiplexer_4 (
    .in0(R0_q), .in1(ram_1_data), .out(multiplexer_4_out), .sel(nor_2_out));

  // Notes on the sheet:
  //   10111
  //   R/W'
  //   01000
  //   PC
  //   contents of rom_1 (hex, n*v repeats v):
  //   21200 33401 45606
  //   11000
  //   MUX
  //   contents of rom_2 (hex, n*v repeats v):
  //   4 1 0 2 0 0 7
  //   if there is no carry, rb stores data from mm
  //   if there is carry, cmg from r0, that is sent to rb
endmodule

module register_file (
  input  [15:0] INPUT,
  input  CLOCK,
  input  READ_WRITE,
  input  [3:0] SELECTBITS4BIT,
  output [15:0] OUTPUT32BIT
);

  wire decoder_1_out0, decoder_1_out1, decoder_1_out2, decoder_1_out3, decoder_1_out4, decoder_1_out5,
       decoder_1_out6, decoder_1_out7, decoder_1_out8, decoder_1_out9, decoder_1_out10, decoder_1_out11,
       decoder_1_out12, decoder_1_out13, decoder_1_out14, decoder_1_out15, not_1_out;
  wire [15:0] R0_q, R1_q, R2_q, R3_q, R4_q, R5_q, R6_q, R7_q, R8_q, R9_q, R10_q, R11_q, R12_q, R13_q, R14_q,
       R15_q;

  not not_1 (not_1_out, READ_WRITE);
  Decoder #(.select(4), .disabled(0)) decoder_1 (
    .out0(decoder_1_out0), .out1(decoder_1_out1), .out2(decoder_1_out2), .out3(decoder_1_out3),
    .out4(decoder_1_out4), .out5(decoder_1_out5), .out6(decoder_1_out6), .out7(decoder_1_out7),
    .out8(decoder_1_out8), .out9(decoder_1_out9), .out10(decoder_1_out10), .out11(decoder_1_out11),
    .out12(decoder_1_out12), .out13(decoder_1_out13), .out14(decoder_1_out14), .out15(decoder_1_out15),
    .sel(SELECTBITS4BIT), .en(not_1_out));
  Register #(.width(16)) R0 (.D(INPUT), .en(decoder_1_out0), .Q(R0_q), .clk(CLOCK));  // open: clr
  Register #(.width(16)) R1 (.D(INPUT), .en(decoder_1_out1), .Q(R1_q), .clk(CLOCK));  // open: clr
  Register #(.width(16)) R2 (.D(INPUT), .en(decoder_1_out2), .Q(R2_q), .clk(CLOCK));  // open: clr
  Register #(.width(16)) R3 (.D(INPUT), .en(decoder_1_out3), .Q(R3_q), .clk(CLOCK));  // open: clr
  Register #(.width(16)) R4 (.D(INPUT), .en(decoder_1_out4), .Q(R4_q), .clk(CLOCK));  // open: clr
  Register #(.width(16)) R5 (.D(INPUT), .en(decoder_1_out5), .Q(R5_q), .clk(CLOCK));  // open: clr
  Register #(.width(16)) R6 (.D(INPUT), .en(decoder_1_out6), .Q(R6_q), .clk(CLOCK));  // open: clr
  Register #(.width(16)) R7 (.D(INPUT), .en(decoder_1_out7), .Q(R7_q), .clk(CLOCK));  // open: clr
  Register #(.width(16)) R8 (.D(INPUT), .en(decoder_1_out8), .Q(R8_q), .clk(CLOCK));  // open: clr
  Register #(.width(16)) R9 (.D(INPUT), .en(decoder_1_out9), .Q(R9_q), .clk(CLOCK));  // open: clr
  Register #(.width(16)) R10 (.D(INPUT), .en(decoder_1_out10), .Q(R10_q), .clk(CLOCK));  // open: clr
  Register #(.width(16)) R11 (.D(INPUT), .en(decoder_1_out11), .Q(R11_q), .clk(CLOCK));  // open: clr
  Register #(.width(16)) R12 (.D(INPUT), .en(decoder_1_out12), .Q(R12_q), .clk(CLOCK));  // open: clr
  Register #(.width(16)) R13 (.D(INPUT), .en(decoder_1_out13), .Q(R13_q), .clk(CLOCK));  // open: clr
  Register #(.width(16)) R14 (.D(INPUT), .en(decoder_1_out14), .Q(R14_q), .clk(CLOCK));  // open: clr
  Register #(.width(16)) R15 (.D(INPUT), .en(decoder_1_out15), .Q(R15_q), .clk(CLOCK));  // open: clr
  Multiplexer #(.select(4), .width(16)) multiplexer_1 (
    .in0(R0_q), .in1(R1_q), .in2(R2_q), .in3(R3_q), .in4(R4_q), .in5(R5_q), .in6(R6_q), .in7(R7_q),
    .in8(R8_q), .in9(R9_q), .in10(R10_q), .in11(R11_q), .in12(R12_q), .in13(R13_q), .in14(R14_q),
    .in15(R15_q), .out(OUTPUT32BIT), .sel(SELECTBITS4BIT), .en(READ_WRITE));
endmodule

module alu (
  input  [15:0] _32_bit_input_A,
  input  [15:0] inputB,
  input  [3:0] opcode,
  input  [3:0] shift_bit,
  output [15:0] carry,
  output [31:0] result
);

  wire adder_1_cout, subtractor_1_bout;
  wire [15:0] adder_2_out, and_1_out, bit_extender_3_out, divider_1_out, divider_1_rem, multiplier_1_cout,
       multiplier_1_out, not_1_out, or_1_out, shifter_1_out, shifter_2_out, shifter_3_out, shifter_4_out,
       subtractor_1_out, subtractor_2_out;
  wire [31:0] adder_1_out, undriven;
  wire [31:16] bit_extender_1_out;

  _7_Segment_Display u_7_segment_display_1 ();  // open: g, f, a, b, e, d, c, dp
  assign bit_extender_1_out = {{15{1'b0}}, 1'b0};  // Bit_Extender bit_extender_1
  Adder #(.width(16)) adder_1 (
    .a(_32_bit_input_A), .b(inputB), .out(adder_1_out[15:0]), .cout(adder_1_cout));  // open: cin
  Subtractor #(.width(16)) subtractor_1 (
    .a(_32_bit_input_A), .b(inputB), .out(subtractor_1_out), .bout(subtractor_1_bout));  // open: bin
  Multiplier #(.width(16)) multiplier_1 (
    .a(_32_bit_input_A), .b(inputB), .out(multiplier_1_out), .cout(multiplier_1_cout));  // open: cin
  Divider #(.width(16)) divider_1 (
    .a(_32_bit_input_A), .b(inputB), .out(divider_1_out), .rem(divider_1_rem));  // open: upper
  assign adder_1_out[31:16] = {{15{1'b0}}, adder_1_cout};  // Bit_Extender bit_extender_2
  assign bit_extender_3_out = {{15{1'b0}}, subtractor_1_bout};  // Bit_Extender bit_extender_3
  Adder #(.width(16)) adder_2 (.a(_32_bit_input_A), .b(16'h1), .out(adder_2_out));  // open: cin, cout
  Subtractor #(.width(16)) subtractor_2 (.a(_32_bit_input_A), .b(16'h1), .out(subtractor_2_out));  // open: bin, bout
  assign not_1_out = ~_32_bit_input_A;  // NOT_Gate not_1, 16 bits wide
  Shifter #(.width(16), .shift("lr")) shifter_1 (.in(_32_bit_input_A), .\dist (shift_bit), .out(shifter_1_out));
  Shifter #(.width(16)) shifter_2 (.in(_32_bit_input_A), .\dist (shift_bit), .out(shifter_2_out));
  Shifter #(.width(16), .shift("rr")) shifter_3 (.in(_32_bit_input_A), .\dist (shift_bit), .out(shifter_3_out));
  Shifter #(.width(16), .shift("rl")) shifter_4 (.in(_32_bit_input_A), .\dist (shift_bit), .out(shifter_4_out));
  assign and_1_out = _32_bit_input_A & inputB;  // AND_Gate and_1, 16 bits wide
  assign or_1_out = _32_bit_input_A | inputB;  // OR_Gate or_1, 16 bits wide
  Multiplexer #(.select(4), .width(32), .enable("false")) multiplexer_1 (
    .in2(adder_1_out), .in3({bit_extender_3_out, subtractor_1_out}),
    .in4({multiplier_1_cout, multiplier_1_out}), .in5({divider_1_rem, divider_1_out}),
    .in6({bit_extender_1_out, adder_2_out}), .in7({bit_extender_1_out, subtractor_2_out}),
    .in8({bit_extender_1_out, and_1_out}), .in9({bit_extender_1_out, or_1_out}),
    .in10({bit_extender_1_out, not_1_out}), .in11({bit_extender_1_out, shifter_1_out}),
    .in12({bit_extender_1_out, shifter_2_out}), .in13({bit_extender_1_out, shifter_3_out}),
    .in14({bit_extender_1_out, shifter_4_out}), .in15(undriven), .out(result), .sel(opcode));  // open: in0, in1
  Multiplexer #(.select(4), .width(16), .enable("false")) multiplexer_2 (
    .in4(multiplier_1_cout), .in5(divider_1_rem), .in15(_32_bit_input_A), .out(carry), .sel(opcode));  // open: in0, in1, in2, in3, in6, in7, in8, in9, in10, in11, in12, in13, in14
endmodule

// PC
module PROGRAMCOUNTER (
  input  [7:0] PC_IN,
  input  CLOCK,
  input  PC_ENABLE,
  output [7:0] OUTPUT
);

  wire [7:0] adder_1_out;

  Adder adder_1 (.a(PC_IN), .b(OUTPUT), .out(adder_1_out), .cin(1'b1));  // open: cout
  Register register_1 (.D(adder_1_out), .en(PC_ENABLE), .Q(OUTPUT), .clk(CLOCK));  // open: clr
endmodule

module load_store (
  input  [15:0] operand_resister,
  input  [15:0] operand_datamemory,
  input  clock,
  input  [3:0] opcode,
  output [15:0] resister,
  output [15:0] datamemory
);

  wire [15:0] multiplexer_1_out, register_1_q;

  Multiplexer #(.width(16), .enable("false")) multiplexer_1 (
    .in0(operand_datamemory), .in1(operand_resister), .out(multiplexer_1_out), .sel(opcode[0]));
  Register #(.width(16)) register_1 (.D(multiplexer_1_out), .Q(register_1_q), .clk(clock));  // open: en, clr
  Demultiplexer #(.width(16), .enable("false")) demultiplexer_1 (
    .out0(resister), .out1(datamemory), .in(register_1_q), .sel(opcode[0]));
endmodule

module shifter (
  input  [15:0] inputfromRB,
  output [3:0] ToALU
);

  Bit_Extender #(.in_width(4), .out_width(1)) bit_extender_1 (.in(inputfromRB[3:0]), .out(ToALU[0]));
  Bit_Extender #(.in_width(4), .out_width(1)) bit_extender_2 (.in(inputfromRB[7:4]), .out(ToALU[1]));
  Bit_Extender #(.in_width(4), .out_width(1)) bit_extender_3 (.in(inputfromRB[11:8]), .out(ToALU[2]));
  Bit_Extender #(.in_width(4), .out_width(1)) bit_extender_4 (.in(inputfromRB[15:12]), .out(ToALU[3]));
endmodule

module programStatusword (
  input  in_1,
  input  CLOCK,
  input  [31:0] RESULTinput,
  input  [15:0] CARRYinput,
  output ZERO,
  output CARRY,
  output SIGN,
  output ODD_PARITY,
  output EVEN_PARITY
);

  wire even_parity_1_out, nor_1_out, nor_2_out, not_1_out, odd_parity_1_out;

  not not_1 (not_1_out, nor_1_out);
  nor nor_1 (nor_1_out, CARRYinput[15], CARRYinput[14], CARRYinput[13], CARRYinput[12], CARRYinput[11], CARRYinput[10], CARRYinput[9], CARRYinput[8], CARRYinput[7], CARRYinput[6], CARRYinput[5], CARRYinput[4], CARRYinput[3], CARRYinput[2], CARRYinput[1], CARRYinput[0]);
  Register #(.width(1)) u_CARRY (.D(not_1_out), .en(in_1), .Q(CARRY), .clk(CLOCK));  // open: clr
  Register #(.width(1)) u_SIGN (.D(RESULTinput[31]), .en(in_1), .Q(SIGN), .clk(CLOCK));  // open: clr
  Register #(.width(1)) u_ZERO (.D(nor_2_out), .en(in_1), .Q(ZERO), .clk(CLOCK));  // open: clr
  nor nor_2 (nor_2_out, RESULTinput[31], RESULTinput[30], RESULTinput[29], RESULTinput[28], RESULTinput[27], RESULTinput[26], RESULTinput[25], RESULTinput[24], RESULTinput[23], RESULTinput[22], RESULTinput[21], RESULTinput[20], RESULTinput[19], RESULTinput[18], RESULTinput[17], RESULTinput[16], RESULTinput[15], RESULTinput[14], RESULTinput[13], RESULTinput[12], RESULTinput[11], RESULTinput[10], RESULTinput[9], RESULTinput[8], RESULTinput[7], RESULTinput[6], RESULTinput[5], RESULTinput[4], RESULTinput[3], RESULTinput[2], RESULTinput[1], RESULTinput[0]);
  xor odd_parity_1 (odd_parity_1_out, RESULTinput[0], RESULTinput[1], RESULTinput[2], RESULTinput[3], RESULTinput[4], RESULTinput[5], RESULTinput[6], RESULTinput[7], RESULTinput[8], RESULTinput[9], RESULTinput[10], RESULTinput[11], RESULTinput[12], RESULTinput[13], RESULTinput[14], RESULTinput[15], RESULTinput[16], RESULTinput[17], RESULTinput[18], RESULTinput[19], RESULTinput[20], RESULTinput[21], RESULTinput[22], RESULTinput[23], RESULTinput[24], RESULTinput[25], RESULTinput[26], RESULTinput[27], RESULTinput[28], RESULTinput[29], RESULTinput[30], RESULTinput[31]);
  Register #(.width(1)) register_1 (.D(odd_parity_1_out), .en(in_1), .Q(ODD_PARITY), .clk(CLOCK));  // open: clr
  xnor even_parity_1 (even_parity_1_out, RESULTinput[0], RESULTinput[1], RESULTinput[2], RESULTinput[3], RESULTinput[4], RESULTinput[5], RESULTinput[6], RESULTinput[7], RESULTinput[8], RESULTinput[9], RESULTinput[10], RESULTinput[11], RESULTinput[12], RESULTinput[13], RESULTinput[14], RESULTinput[15], RESULTinput[16], RESULTinput[17], RESULTinput[18], RESULTinput[19], RESULTinput[20], RESULTinput[21], RESULTinput[22], RESULTinput[23], RESULTinput[24], RESULTinput[25], RESULTinput[26], RESULTinput[27], RESULTinput[28], RESULTinput[29], RESULTinput[30], RESULTinput[31]);
  Register #(.width(1)) register_2 (.D(even_parity_1_out), .en(in_1), .Q(EVEN_PARITY), .clk(CLOCK));  // open: clr
endmodule
