// Logisim project 32 BIT PROCESSOR (ONE ADDRESS, INDIRECT ADDRESSING).circ as structural Verilog: 12 circuits, main circuit FULLV1
module ALU (
  input  [3:0] OpCode,
  input  [31:0] Input1,
  input  [31:0] Input2,
  output [31:0] Output,
  output Overflow,
  output Negative
);

  wire [31:0] adder_1_out, adder_2_out, and_1_out, divider_1_out, multiplier_1_out, not_1_out, or_1_out,
       shifter_1_out, shifter_2_out, shifter_3_out, shifter_4_out, subtractor_1_out, subtractor_2_out;

  assign not_1_out = ~Input1;  // NOT_Gate not_1, 32 bits wide
  Multiplier #(.width(32)) multiplier_1 (.a(Input1), .b(Input2), .out(multiplier_1_out));  // open: cin, cout
  Divider #(.width(32)) divider_1 (.a(Input1), .b(Input2), .out(divider_1_out));  // open: upper, rem
  Shifter #(.width(32)) shifter_1 (.in(Input1), .\dist (5'b00001), .out(shifter_1_out));
  Shifter #(.width(32), .shift("lr")) shifter_2 (.in(Input1), .\dist (5'b00001), .out(shifter_2_out));
  Shifter #(.width(32), .shift("rl")) shifter_3 (.in(Input1), .\dist (5'b00001), .out(shifter_3_out));
  Shifter #(.width(32), .shift("rr")) shifter_4 (.in(Input1), .\dist (5'b00001), .out(shifter_4_out));
  Adder #(.width(32)) adder_1 (.a(Input1), .b(32'h1), .out(adder_1_out));  // open: cin, cout
  Subtractor #(.width(32)) subtractor_1 (.a(Input1), .b(32'h1), .out(subtractor_1_out));  // open: bin, bout
  assign or_1_out = Input1 | Input2;  // OR_Gate or_1, 32 bits wide
  assign and_1_out = Input2 & Input1;  // AND_Gate and_1, 32 bits wide
  Adder #(.width(32)) adder_2 (.a(Input2), .b(Input1), .out(adder_2_out), .cout(Overflow));  // open: cin
  Subtractor #(.width(32)) subtractor_2 (.a(Input1), .b(Input2), .out(subtractor_2_out), .bout(Negative));  // open: bin
  Multiplexer #(.select(4), .width(32), .enable("false")) multiplexer_1 (
    .in0(Input2), .in1(Input1), .in2(adder_2_out), .in3(subtractor_2_out), .in4(multiplier_1_out),
    .in5(divider_1_out), .in6(adder_1_out), .in7(subtractor_1_out), .in8(and_1_out), .in9(or_1_out),
    .in10(not_1_out), .in11(Input2), .in12(shifter_2_out), .in13(shifter_1_out), .in14(shifter_4_out),
    .in15(shifter_3_out), .out(Output), .sel(OpCode));
  // Probe on Output

  // Notes on the sheet:
  //   Designed By Vignesh Chougule
endmodule

module Direct_Addressing_With_PC (
  output [31:0] Accumulator_Content
);

  wire clock_1_out, multiplexer_1_out, multiplexer_2_out;
  wire [15:0] PC_INC_out_3, ram_1_data;
  wire [31:0] ALU_output, controlled_buffer_1_out, ram_2_data;

  Clock clock_1 (.out(clock_1_out));
  PC PC_INC (.Clock(clock_1_out), .out_3(PC_INC_out_3));  // open: PCRESET
  RAM #(.addrWidth(16), .dataWidth(16)) ram_1 (.addr(PC_INC_out_3), .data(ram_1_data));  // open: sel, clk, ld, clr
  Multiplexer #(.select(4), .enable("false")) multiplexer_1 (
    .in0(1'b0), .in1(1'b0), .in2(1'b0), .in3(1'b0), .in4(1'b0), .in5(1'b0), .in6(1'b0), .in7(1'b0),
    .in8(1'b0), .in9(1'b0), .in10(1'b0), .in11(1'b1), .in12(1'b0), .in13(1'b0), .in14(1'b0), .in15(1'b0),
    .out(multiplexer_1_out), .sel(ram_1_data[3:0]));
  assign controlled_buffer_1_out = multiplexer_1_out ? Accumulator_Content : 32'bz;  // Controlled_Buffer controlled_buffer_1
  Register #(.width(32)) Accumulator (.D(ALU_output), .Q(Accumulator_Content), .clk(clock_1_out));  // open: en, clr
  assign controlled_buffer_1_out = multiplexer_2_out ? ALU_output : 32'bz;  // Controlled_Buffer controlled_buffer_2
  RAM #(.addrWidth(12), .dataWidth(32), .bus("separate")) ram_2 (
    .addr(ram_1_data[15:4]), .din(controlled_buffer_1_out), .data(ram_2_data), .clk(clock_1_out));  // open: str, sel, ld, clr
  ALU ALU (
    .Input1(Accumulator_Content), .Input2(ram_2_data), .OpCode(ram_1_data[3:0]), .Output(ALU_output));  // open: Overflow, Negative
  Multiplexer #(.select(4), .enable("false")) multiplexer_2 (
    .in0(1'b1), .in1(1'b1), .in2(1'b1), .in3(1'b1), .in4(1'b1), .in5(1'b1), .in6(1'b1), .in7(1'b1),
    .in8(1'b1), .in9(1'b1), .in10(1'b1), .in11(1'b0), .in12(1'b1), .in13(1'b1), .in14(1'b1), .in15(1'b1),
    .out(multiplexer_2_out), .sel(ram_1_data[3:0]));

  // Notes on the sheet:
  //   0
  //   1
  //   2
  //   3
  //   4
  //   5
  //   6
  //   7
  //   8
  //   9
  //   a
  //   b
  //   c
  //   d
  //   e
  //   f
  //   0000
  //   0001
  //   0010
  //   0011
  //   0100
  //   0101
  //   0110
  //   0111
  //   1000
  //   1001
  //   1010
  //   1011
  //   EXCHANGE
  //   1100
  //   SHIFTRIGHT
  //   1101
  //   SHIFTLEFT
  //   1110
  //   1111
  //   OPCODE
  //   LOAD
  //   STORE
  //   ADD
  //   SUB
  //   MUL
  //   DIV
  //   INC
  //   DEC
  //   AND
  //   OR
  //   NOT
  //   ROR
  //   LOR
  //   32 BIT PROCESSOR (ONE ADDRESS, DIRECT ADDRESSING)
  //   KLE TECHNOLOGICAL UNIVERSITY HUBLI
  //   F DIVISION CS(AI) 2024
  //   F1 BATCH
  //   Designed by:
  //   Vignesh Chougule: 01FE22BCI
  //   Nihal Jain: 01FE22BCI
  //   Aradhya Gaonkar: 01FE22BCI019
  //   Nikhil Deshpande: 01FE22BCI
endmodule

module PC (
  input  PCRESET,
  input  Clock,
  output [15:0] out_3
);

  wire [15:0] adder_1_out;

  Adder #(.width(16)) adder_1 (.a(out_3), .b(16'h1), .out(adder_1_out));  // open: cin, cout
  Register #(.width(16)) register_1 (.D(adder_1_out), .Q(out_3), .clk(Clock), .clr(PCRESET));  // open: en
endmodule

module main (
);


  // Notes on the sheet:
  //   0000
  //   0
  //   0001
  //   1
  //   0010
  //   2
  //   3
  //   0011
  //   0100
  //   4
  //   0101
  //   5
  //   0110
  //   6
  //   0111
  //   7
  //   1000
  //   8
  //   1001
  //   9
  //   1010
  //   a
  //   b
  //   1011
  //   c
  //   1100
  //   1101
  //   d
  //   e
  //   1110
  //   1111
  //   f
  //   LOAD
  //   STORE
  //   ADD
  //   SUB
  //   MUL
  //   DIV
  //   INC
  //   DEC
  //   AND
  //   OR
  //   NOT
  //   EXCHANGE
  //   SHIFTRIGHT
  //   SHIFTLEFT
  //   ROR
  //   LOR
  //   OPCODE
endmodule

module EXPERIMENT (
  input  [11:0] in_1,
  input  in_2
);

  wire [11:0] multiplexer_1_out, register_1_q;
  wire [31:0] ram_1_data, register_2_q;
  wire [31:12] register_1_q_2;

  Multiplexer #(.width(12), .enable("false")) multiplexer_1 (
    .in0(in_1), .in1(register_1_q), .out(multiplexer_1_out), .sel(in_2));
  RAM #(.addrWidth(12), .dataWidth(32)) ram_1 (
    .addr(multiplexer_1_out), .data(ram_1_data), .clk(in_2));  // open: sel, ld, clr
  Register #(.width(32)) register_1 (.D(ram_1_data), .Q({register_1_q_2, register_1_q}), .clk(in_2));  // open: en, clr
  Register #(.width(32), .trigger("falling")) register_2 (
    .D(ram_1_data), .Q(register_2_q), .clk(in_2));  // open: en, clr
  // Probe on register_2_q
endmodule

module SUBCIRCUIT (
  input  [15:0] CodeD,
  input  Clock,
  input  [31:0] RightD,
  output [15:0] CodeA,
  output [15:0] IR,
  output [15:0] PC,
  output [11:0] MAR,
  output [15:0] Fetched,
  output ZeroFlag,
  output Negative,
  output [15:0] Executed,
  output [31:0] AC,
  output [11:0] A,
  output Overflow,
  output [31:0] LowerD,
  output ClockTomem,
  output [31:0] MBR,
  output EvenParity,
  output OddParity
);

  wire ALU_negative, ALU_overflow, comparator_1_eq, comparator_1_gt, comparator_1_lt, comparator_3_eq,
       comparator_3_gt, comparator_3_lt, comparator_4_eq, comparator_4_gt, comparator_4_lt,
       controlled_buffer_1_out, controlled_buffer_5_out, controlled_buffer_7_out, multiplexer_1_out,
       multiplexer_2_out, or_1_out, or_2_out, or_3_out;
  wire [3:0] register_1_q;
  wire [15:0] pc_1_out_3;
  wire [31:0] ALU_output;

  TEMP3 temp3_1 (.in_1(Clock), .out_2(CodeA));
  PC pc_1 (.Clock(Clock), .out_3(pc_1_out_3));  // open: PCRESET
  Comparator #(.width(16)) comparator_1 (
    .a(pc_1_out_3), .b(16'h1), .gt(comparator_1_gt), .eq(comparator_1_eq), .lt(comparator_1_lt));
  Shift_Register #(.width(16), .length(2), .trigger("falling")) shift_register_1 (
    .shift(controlled_buffer_1_out), .in(CodeD), .clk(Clock), .out(Executed), .q0(Fetched));  // open: load, clr, d0, d1, q1
  or or_1 (or_1_out, comparator_1_gt, comparator_1_eq);
  assign controlled_buffer_1_out = or_1_out ? or_1_out : 1'bz;  // Controlled_Buffer controlled_buffer_1
  assign controlled_buffer_1_out = comparator_1_lt ? 1'b0 : 1'bz;  // Controlled_Buffer controlled_buffer_2
  Register #(.width(4), .trigger("high")) register_1 (.D(CodeD[3:0]), .Q(register_1_q), .clk(1'b1));  // open: en, clr
  Register #(.width(12), .trigger("high")) register_2 (.D(CodeD[15:4]), .Q(MAR), .clk(1'b1));  // open: en, clr
  Register #(.width(16), .trigger("high")) register_3 (
    .D({MAR, register_1_q}), .Q({A, IR[3:0]}), .clk(1'b1));  // open: en, clr
  Multiplexer #(.select(4), .enable("false")) multiplexer_1 (
    .in0(1'b0), .in1(1'b0), .in2(1'b0), .in3(1'b0), .in4(1'b0), .in5(1'b0), .in6(1'b0), .in7(1'b0),
    .in8(1'b0), .in9(1'b0), .in10(1'b0), .in11(1'b1), .in12(1'b0), .in13(1'b0), .in14(1'b0), .in15(1'b0),
    .out(multiplexer_1_out), .sel(IR[3:0]));
  Register #(.width(32), .trigger("high")) register_4 (.D(LowerD), .Q(MBR), .clk(1'b1));  // open: en, clr
  assign LowerD = multiplexer_1_out ? AC : 32'bz;  // Controlled_Buffer controlled_buffer_3
  Register #(.width(32)) Accumulator (.D(ALU_output), .Q(AC), .clk(Clock));  // open: en, clr
  assign LowerD = multiplexer_2_out ? ALU_output : 32'bz;  // Controlled_Buffer controlled_buffer_4
  ALU ALU (
    .Input1(AC), .Input2(RightD), .OpCode(IR[3:0]), .Output(ALU_output), .Overflow(ALU_overflow),
    .Negative(ALU_negative));
  Multiplexer #(.select(4), .enable("false")) multiplexer_2 (
    .in0(1'b1), .in1(1'b1), .in2(1'b1), .in3(1'b1), .in4(1'b1), .in5(1'b1), .in6(1'b1), .in7(1'b1),
    .in8(1'b1), .in9(1'b1), .in10(1'b1), .in11(1'b0), .in12(1'b1), .in13(1'b1), .in14(1'b1), .in15(1'b1),
    .out(multiplexer_2_out), .sel(IR[3:0]));
  Comparator #(.width(32)) comparator_2 (.a(AC), .b({32{1'b0}}), .eq(ZeroFlag));  // open: gt, lt
  Comparator #(.width(4)) comparator_3 (
    .a(IR[3:0]), .b(4'b0011), .gt(comparator_3_gt), .eq(comparator_3_eq), .lt(comparator_3_lt));
  or or_2 (or_2_out, comparator_3_gt, comparator_3_lt);
  assign controlled_buffer_5_out = comparator_3_eq ? ALU_negative : 1'bz;  // Controlled_Buffer controlled_buffer_5
  assign controlled_buffer_5_out = or_2_out ? 1'b0 : 1'bz;  // Controlled_Buffer controlled_buffer_6
  Comparator #(.width(4)) comparator_4 (
    .a(IR[3:0]), .b(4'b0010), .gt(comparator_4_gt), .eq(comparator_4_eq), .lt(comparator_4_lt));
  or or_3 (or_3_out, comparator_4_gt, comparator_4_lt);
  assign controlled_buffer_7_out = comparator_4_eq ? ALU_overflow : 1'bz;  // Controlled_Buffer controlled_buffer_7
  xnor even_parity_1 (EvenParity, AC[0], AC[1], AC[2], AC[3], AC[4], AC[5], AC[6], AC[7], AC[8], AC[9], AC[10], AC[11], AC[12], AC[13], AC[14], AC[15], AC[16], AC[17], AC[18], AC[19], AC[20], AC[21], AC[22], AC[23], AC[24], AC[25], AC[26], AC[27], AC[28], AC[29], AC[30], AC[31]);
  Register #(.width(1)) register_5 (.D(controlled_buffer_5_out), .Q(Negative), .clk(Clock));  // open: en, clr
  assign controlled_buffer_7_out = or_3_out ? 1'b0 : 1'bz;  // Controlled_Buffer controlled_buffer_8
  Register #(.width(1)) register_6 (.D(controlled_buffer_7_out), .Q(Overflow), .clk(Clock));  // open: en, clr
  xor odd_parity_1 (OddParity, AC[0], AC[1], AC[2], AC[3], AC[4], AC[5], AC[6], AC[7], AC[8], AC[9], AC[10], AC[11], AC[12], AC[13], AC[14], AC[15], AC[16], AC[17], AC[18], AC[19], AC[20], AC[21], AC[22], AC[23], AC[24], AC[25], AC[26], AC[27], AC[28], AC[29], AC[30], AC[31]);

  assign ClockTomem = Clock;
  assign IR[15:4] = A;
  assign PC = CodeA;

  // Notes on the sheet:
  //   0000
  //   0
  //   0001
  //   1
  //   0010
  //   2
  //   3
  //   0011
  //   4
  //   0100
  //   0101
  //   5
  //   0110
  //   6
  //   0111
  //   7
  //   1000
  //   8
  //   1001
  //   9
  //   1010
  //   a
  //   b
  //   1011
  //   c
  //   1100
  //   1101
  //   d
  //   e
  //   1110
  //   1111
  //   f
  //   LOAD
  //   STORE
  //   ADD
  //   SUB
  //   MUL
  //   DIV
  //   INC
  //   DEC
  //   AND
  //   OR
  //   NOT
  //   EXCHANGE
  //   SHIFTRIGHT
  //   SHIFTLEFT
  //   ROR
  //   LOR
  //   OPCODE
  //   32 BIT PROCESSOR (ONE ADDRESS, DIRECT ADDRESSING)
  //   KLE TECHNOLOGICAL UNIVERSITY HUBLI
  //   F DIVISION CS(AI) 2024
  //   F1 BATCH
  //   Designed by:
  //   Vignesh Chougule: 01FE22BCI
  //   Nihal Jain: 01FE22BCI
  //   Aradhya Gaonkar: 01FE22BCI019
  //   Nikhil Deshpande: 01FE22BCI
endmodule

module FULLV1 (
  output EvenParity,
  output Zero,
  output OverFlow,
  output Negative,
  output OddParity
);

  wire clock_1_out, emergency_1_out, indirectmaker_1_clocktomem, indirectmaker_1_seltomem, not_1_out,
       subcircuit_1_clocktomem;
  wire [11:0] indirectmaker_1_atomem, subcircuit_1_a, subcircuit_1_mar;
  wire [15:0] ram_1_data, subcircuit_1_codea, subcircuit_1_executed, subcircuit_1_fetched, subcircuit_1_ir,
       subcircuit_1_pc;
  wire [31:0] indirectmaker_1_douttomem, indirectmaker_1_onclockcycle, ram_2_data, subcircuit_1_ac,
       subcircuit_1_lowerd, subcircuit_1_mbr;

  EMERGENCY emergency_1 (.Clock(clock_1_out), .OUT(emergency_1_out));
  Clock clock_1 (.out(clock_1_out));
  Clock clock_2 ();  // open: out
  // Probe on subcircuit_1_pc
  // Probe on subcircuit_1_ir
  // Probe on subcircuit_1_ac
  SUBCIRCUIT subcircuit_1 (
    .RightD(indirectmaker_1_onclockcycle), .IR(subcircuit_1_ir), .PC(subcircuit_1_pc),
    .MAR(subcircuit_1_mar), .AC(subcircuit_1_ac), .A(subcircuit_1_a), .LowerD(subcircuit_1_lowerd),
    .MBR(subcircuit_1_mbr), .ClockTomem(subcircuit_1_clocktomem), .CodeA(subcircuit_1_codea),
    .CodeD(ram_1_data), .Clock(emergency_1_out), .ZeroFlag(Zero), .Overflow(OverFlow), .Negative(Negative),
    .EvenParity(EvenParity), .OddParity(OddParity), .Fetched(subcircuit_1_fetched),
    .Executed(subcircuit_1_executed));
  RAM #(.addrWidth(16), .dataWidth(16)) ram_1 (
    .addr(subcircuit_1_codea), .data(ram_1_data));  // open: sel, clk, ld, clr
  not not_1 (not_1_out, emergency_1_out);
  // Probe on subcircuit_1_mar
  // Probe on subcircuit_1_mbr
  // Probe on subcircuit_1_fetched
  // Probe on subcircuit_1_executed
  INDIRECTMAKER indirectmaker_1 (
    .D2toMem(ram_2_data), .A(subcircuit_1_a), .Indirecter(not_1_out), .DtoMem(subcircuit_1_lowerd),
    .AtoMem(indirectmaker_1_atomem), .OnClockCycle(indirectmaker_1_onclockcycle),
    .DoutTomem(indirectmaker_1_douttomem), .SelToMem(indirectmaker_1_seltomem),
    .ClockToMem(indirectmaker_1_clocktomem), .ClockMem(subcircuit_1_clocktomem));  // open: AfterClockCycle, SelMem
  RAM #(.addrWidth(12), .dataWidth(32), .bus("separate")) ram_2 (
    .addr(indirectmaker_1_atomem), .din(indirectmaker_1_douttomem), .data(ram_2_data),
    .sel(indirectmaker_1_seltomem), .clk(indirectmaker_1_clocktomem));  // open: str, ld, clr

  // Other names for the same wires on the sheet: EP = EvenParity; N = Negative; O = OverFlow; OP = OddParity;
  //   Z = Zero

  // Notes on the sheet:
  //   Designed by:
  //   Vignesh Chougule: 01FE22BCI
  //   Nihal Jain: 01FE22BCI
  //   Aradhya Gaonkar: 01FE22BCI019
  //   Nikhil Deshpande: 01FE22BCI
  //   CodeMemory
  //   32 BIT PROCESSOR (ONE ADDRESS, INDIRECT ADDRESSING)
  //   CPU
  //   PSW
  //   KLE TECHNOLOGICAL UNIVERSITY HUBLI
  //   F DIVISION CS(AI) 2024
  //   DataMemory
  //   INDIRECTOR
  //   F1 BATCH
  //   0
  //   1
  //   2
  //   3
  //   4
  //   5
  //   6
  //   7
  //   8
  //   9
  //   a
  //   b
  //   c
  //   d
  //   e
  //   f
  //   0000
  //   0001
  //   0010
  //   0011
  //   0100
  //   0101
  //   0110
  //   0111
  //   1000
  //   1001
  //   1010
  //   EXCHANGE
  //   1011
  //   1100
  //   SHIFTRIGHT
  //   1101
  //   SHIFTLEFT
  //   1110
  //   1111
  //   OPCODE
  //   LOAD
  //   STORE
  //   ADD
  //   SUB
  //   MUL
  //   DIV
  //   INC
  //   DEC
  //   AND
  //   OR
  //   NOT
  //   ROR
  //   LOR
endmodule

module INDIRECTMAKER (
  input  [31:0] D2toMem,
  input  [11:0] A,
  input  Indirecter,
  input  SelMem,
  input  ClockMem,
  input  [31:0] DtoMem,
  output [11:0] AtoMem,
  output [31:0] OnClockCycle,
  output SelToMem,
  output ClockToMem,
  output [31:0] AfterClockCycle,
  output [31:0] DoutTomem
);

  wire [11:0] register_1_q;
  wire [31:12] register_1_q_2;

  Multiplexer #(.width(12), .enable("false")) multiplexer_1 (
    .in0(A), .in1(register_1_q), .out(AtoMem), .sel(Indirecter));
  Register #(.width(32)) register_1 (
    .D(D2toMem), .Q({register_1_q_2, register_1_q}), .clk(Indirecter));  // open: en, clr
  Register #(.width(32), .trigger("falling")) register_2 (
    .D(D2toMem), .Q(AfterClockCycle), .clk(Indirecter));  // open: en, clr
  // Probe on AfterClockCycle

  assign ClockToMem = ClockMem;
  assign DoutTomem = DtoMem;
  assign OnClockCycle = D2toMem;
  assign SelToMem = SelMem;

  // Notes on the sheet:
  //   Designed By Aradhya. A. Gaonkar
endmodule

module NEWEST (
  output [31:0] Accumulator_Content
);

  wire clock_1_out, multiplexer_1_out, multiplexer_2_out;
  wire [3:0] register_3_q;
  wire [11:0] register_2_q;
  wire [15:0] ram_1_data, register_1_q, temp3_1_out_2;
  wire [15:4] register_3_q_2;
  wire [31:0] ALU_output, controlled_buffer_1_out, ram_2_data, register_4_q;

  Clock clock_1 (.out(clock_1_out));
  TEMP3 temp3_1 (.in_1(clock_1_out), .out_2(temp3_1_out_2));
  Register #(.width(16)) register_1 (.D(ram_1_data), .Q(register_1_q), .clk(clock_1_out));  // open: en, clr
  RAM #(.addrWidth(16), .dataWidth(16)) ram_1 (.addr(temp3_1_out_2), .data(ram_1_data));  // open: sel, clk, ld, clr
  Register #(.width(12), .trigger("high")) register_2 (
    .D(register_1_q[15:4]), .Q(register_2_q), .clk(1'b1));  // open: en, clr
  Multiplexer #(.select(4), .enable("false")) multiplexer_1 (
    .in0(1'b0), .in1(1'b0), .in2(1'b0), .in3(1'b0), .in4(1'b0), .in5(1'b0), .in6(1'b0), .in7(1'b0),
    .in8(1'b0), .in9(1'b0), .in10(1'b0), .in11(1'b1), .in12(1'b0), .in13(1'b0), .in14(1'b0), .in15(1'b0),
    .out(multiplexer_1_out), .sel(register_3_q));
  Register #(.width(16), .trigger("high")) register_3 (
    .D({register_2_q, register_1_q[3:0]}), .Q({register_3_q_2, register_3_q}), .clk(1'b1));  // open: en, clr
  assign controlled_buffer_1_out = multiplexer_1_out ? Accumulator_Content : 32'bz;  // Controlled_Buffer controlled_buffer_1
  Register #(.width(32), .trigger("high")) register_4 (
    .D(controlled_buffer_1_out), .Q(register_4_q), .clk(1'b1));  // open: en, clr
  Register #(.width(32)) Accumulator (.D(ALU_output), .Q(Accumulator_Content), .clk(clock_1_out));  // open: en, clr
  assign controlled_buffer_1_out = multiplexer_2_out ? ALU_output : 32'bz;  // Controlled_Buffer controlled_buffer_2
  RAM #(.addrWidth(12), .dataWidth(32), .bus("separate")) ram_2 (
    .addr(register_3_q_2), .din(register_4_q), .data(ram_2_data), .clk(clock_1_out));  // open: str, sel, ld, clr
  ALU ALU (
    .Input1(Accumulator_Content), .Input2(ram_2_data), .OpCode(register_3_q), .Output(ALU_output));  // open: Overflow, Negative
  Multiplexer #(.select(4), .enable("false")) multiplexer_2 (
    .in0(1'b1), .in1(1'b1), .in2(1'b1), .in3(1'b1), .in4(1'b1), .in5(1'b1), .in6(1'b1), .in7(1'b1),
    .in8(1'b1), .in9(1'b1), .in10(1'b1), .in11(1'b0), .in12(1'b1), .in13(1'b1), .in14(1'b1), .in15(1'b1),
    .out(multiplexer_2_out), .sel(register_3_q));

  // Notes on the sheet:
  //   0
  //   1
  //   2
  //   3
  //   4
  //   5
  //   6
  //   7
  //   8
  //   9
  //   a
  //   b
  //   c
  //   d
  //   e
  //   f
  //   0000
  //   0001
  //   0010
  //   0011
  //   0100
  //   0101
  //   0110
  //   0111
  //   1000
  //   1001
  //   1010
  //   EXCHANGE
  //   1011
  //   1100
  //   SHIFTRIGHT
  //   1101
  //   SHIFTLEFT
  //   1110
  //   1111
  //   OPCODE
  //   LOAD
  //   STORE
  //   ADD
  //   SUB
  //   MUL
  //   DIV
  //   INC
  //   DEC
  //   AND
  //   OR
  //   NOT
  //   ROR
  //   LOR
  //   32 BIT PROCESSOR (ONE ADDRESS, DIRECT ADDRESSING)
  //   KLE TECHNOLOGICAL UNIVERSITY HUBLI
  //   F DIVISION CS(AI) 2024
  //   F1 BATCH
  //   Designed by:
  //   Vignesh Chougule: 01FE22BCI
  //   Nihal Jain: 01FE22BCI
  //   Aradhya Gaonkar: 01FE22BCI019
  //   Nikhil Deshpande: 01FE22BCI
endmodule

module FULLDIRECT (
);

  wire clock_1_out, subcircuit_1_clocktomem;
  wire [11:0] subcircuit_1_a, subcircuit_1_mar;
  wire [15:0] ram_1_data, subcircuit_1_codea, subcircuit_1_ir, subcircuit_1_pc;
  wire [31:0] ram_2_data, subcircuit_1_ac, subcircuit_1_lowerd, subcircuit_1_mbr;

  // Probe on subcircuit_1_ir
  // Probe on subcircuit_1_pc
  RAM #(.addrWidth(16), .dataWidth(16)) ram_1 (
    .addr(subcircuit_1_codea), .data(ram_1_data));  // open: sel, clk, ld, clr
  // Probe on subcircuit_1_ac
  SUBCIRCUIT subcircuit_1 (
    .RightD(ram_2_data), .IR(subcircuit_1_ir), .PC(subcircuit_1_pc), .MAR(subcircuit_1_mar),
    .AC(subcircuit_1_ac), .A(subcircuit_1_a), .LowerD(subcircuit_1_lowerd), .MBR(subcircuit_1_mbr),
    .ClockTomem(subcircuit_1_clocktomem), .CodeA(subcircuit_1_codea), .CodeD(ram_1_data), .Clock(clock_1_out));  // open: ZeroFlag, Overflow, Negative, EvenParity, OddParity, Fetched, Executed
  Clock clock_1 (.out(clock_1_out));
  // Probe on subcircuit_1_mbr
  // Probe on subcircuit_1_mar
  RAM #(.addrWidth(12), .dataWidth(32), .bus("separate")) ram_2 (
    .addr(subcircuit_1_a), .din(subcircuit_1_lowerd), .data(ram_2_data), .clk(subcircuit_1_clocktomem));  // open: str, sel, ld, clr
endmodule

module TEMP3 (
  input  in_1,
  output [15:0] out_2
);

  wire comparator_1_eq, comparator_1_gt, comparator_1_lt, or_1_out;
  wire [15:0] controlled_buffer_1_out, pc_1_out_3, subtractor_1_out;

  PC pc_1 (.Clock(in_1), .out_3(pc_1_out_3));  // open: PCRESET
  Comparator #(.width(16)) comparator_1 (
    .a(pc_1_out_3), .b(16'h2), .gt(comparator_1_gt), .eq(comparator_1_eq), .lt(comparator_1_lt));
  assign controlled_buffer_1_out = or_1_out ? pc_1_out_3 : 16'bz;  // Controlled_Buffer controlled_buffer_1
  or or_1 (or_1_out, comparator_1_gt, comparator_1_eq);
  Subtractor #(.width(16)) subtractor_1 (
    .a(controlled_buffer_1_out), .b(16'h1), .out(subtractor_1_out));  // open: bin, bout
  assign out_2 = comparator_1_lt ? {16{1'b0}} : 16'bz;  // Controlled_Buffer controlled_buffer_2
  assign out_2 = or_1_out ? subtractor_1_out : 16'bz;  // Controlled_Buffer controlled_buffer_3
endmodule

module EMERGENCY (
  input  Clock,
  output OUT
);

  wire comparator_1_eq, comparator_2_eq;
  wire [15:0] pc_1_out_3;

  PC pc_1 (.PCRESET(comparator_2_eq), .Clock(Clock), .out_3(pc_1_out_3));
  Comparator #(.width(16)) comparator_1 (.a(pc_1_out_3), .b(16'h4), .eq(comparator_1_eq));  // open: gt, lt
  Comparator #(.width(16)) comparator_2 (.a(pc_1_out_3), .b(16'h5), .eq(comparator_2_eq));  // open: gt, lt
  // Probe on pc_1_out_3
  or or_1 (OUT, comparator_1_eq, comparator_2_eq);
endmodule
