// Logisim project 8-bit processor.circ as structural Verilog: 3 circuits, main circuit main
module main (
);

  wire clock_1_out;
  wire [3:0] Register_file_p3, Register_file_p4;
  wire [11:0] IR_q, MAR_q, MBR_q, rom_1_data;

  Register #(.width(12)) MAR (.Q(MAR_q), .clk(clock_1_out));  // open: D, en, clr
  Clock clock_1 (.out(clock_1_out));
  ROM #(.addrWidth(12), .dataWidth(12)) rom_1 (.addr(MAR_q), .data(rom_1_data));  // open: sel
  Register #(.width(12)) MBR (.D(rom_1_data), .Q(MBR_q), .clk(clock_1_out));  // open: en, clr
  Register #(.width(12)) IR (.D(MBR_q), .Q(IR_q), .clk(clock_1_out));  // open: en, clr
  // Register_File Register_file: pin names not known; wires that end beside it: clock_1_out, IR_q[7:0], Register_file_p3, Register_file_p4
  Register #(.width(4)) register_1 (.D(Register_file_p3), .Q(Register_file_p4), .clk(clock_1_out));  // open: en, clr
  RAM #(.addrWidth(4), .dataWidth(4), .bus("separate")) ram_1 (
    .addr(Register_file_p4), .clk(clock_1_out));  // open: din, data, str, sel, ld, clr
endmodule

module Program_Counter (
  input  [7:0] in_1,
  input  PC_Enable,
  input  PC_reset,
  input  Clock,
  output [7:0] out_5
);

  wire [7:0] adder_1_out;

  Adder adder_1 (.a(in_1), .b(out_5), .out(adder_1_out), .cin(1'b1));  // open: cout
  Register register_1 (.D(adder_1_out), .en(PC_Enable), .Q(out_5), .clk(Clock), .clr(PC_reset));
  Hex_Digit_Display hex_digit_display_1 (.value(out_5[7:4]));  // open: dp
  Hex_Digit_Display hex_digit_display_2 (.value(out_5[3:0]));  // open: dp

  // Notes on the sheet:
  //   Program Counter
endmodule

module Register_File (
  input  [2:0] in_1,
  input  [2:0] in_2,
  input  in_3
);

  wire and_1_out, and_2_out, and_3_out, and_4_out, and_5_out, and_6_out, and_7_out, and_8_out, and_9_out,
       and_10_out, and_11_out, and_12_out, and_13_out, and_14_out, and_15_out, and_16_out, clock_1_out,
       decoder_1_out0, decoder_1_out1, decoder_1_out2, decoder_1_out3, decoder_1_out4, decoder_1_out5,
       decoder_1_out6, decoder_1_out7, decoder_1_out8, decoder_1_out9, decoder_1_out10, decoder_1_out11,
       decoder_1_out12, decoder_1_out13, decoder_1_out14, decoder_1_out15;
  wire [3:0] undriven;
  wire [7:0] multiplexer_1_out, multiplexer_2_out, register_1_q, register_2_q, register_3_q, register_4_q,
       register_5_q, register_6_q, register_7_q, register_8_q, undriven_2;

  Decoder #(.select(4)) decoder_1 (
    .out0(decoder_1_out0), .out1(decoder_1_out1), .out2(decoder_1_out2), .out3(decoder_1_out3),
    .out4(decoder_1_out4), .out5(decoder_1_out5), .out6(decoder_1_out6), .out7(decoder_1_out7),
    .out8(decoder_1_out8), .out9(decoder_1_out9), .out10(decoder_1_out10), .out11(decoder_1_out11),
    .out12(decoder_1_out12), .out13(decoder_1_out13), .out14(decoder_1_out14), .out15(decoder_1_out15),
    .sel(undriven));  // open: en
  Clock clock_1 (.out(clock_1_out));
  and and_1 (and_1_out, decoder_1_out0, in_3);
  and and_2 (and_2_out, decoder_1_out1, in_3);
  and and_3 (and_3_out, decoder_1_out2, in_3);
  and and_4 (and_4_out, decoder_1_out3, in_3);
  and and_5 (and_5_out, decoder_1_out4, in_3);
  and and_6 (and_6_out, decoder_1_out5, in_3);
  and and_7 (and_7_out, decoder_1_out6, in_3);
  and and_8 (and_8_out, decoder_1_out7, in_3);
  and and_9 (and_9_out, decoder_1_out8, in_3);
  and and_10 (and_10_out, decoder_1_out9, in_3);
  and and_11 (and_11_out, decoder_1_out10, in_3);
  and and_12 (and_12_out, decoder_1_out11, in_3);
  and and_13 (and_13_out, decoder_1_out12, in_3);
  and and_14 (and_14_out, decoder_1_out13, in_3);
  and and_15 (and_15_out, decoder_1_out14, in_3);
  and and_16 (and_16_out, decoder_1_out15, in_3);
  Register register_1 (.D(undriven_2), .en(clock_1_out), .Q(register_1_q), .clr(and_1_out));  // open: clk
  Register register_2 (.D(undriven_2), .Q(register_2_q), .clk(clock_1_out), .clr(and_2_out));  // open: en
  Register register_3 (.D(undriven_2), .Q(register_3_q), .clk(clock_1_out), .clr(and_3_out));  // open: en
  Register register_4 (.D(undriven_2), .Q(register_4_q), .clk(clock_1_out), .clr(and_4_out));  // open: en
  Register register_5 (.D(undriven_2), .Q(register_5_q), .clk(clock_1_out), .clr(and_5_out));  // open: en
  Register register_6 (.D(undriven_2), .Q(register_6_q), .clk(clock_1_out), .clr(and_6_out));  // open: en
  Register register_7 (.D(undriven_2), .Q(register_7_q), .clk(clock_1_out), .clr(and_7_out));  // open: en
  Register register_8 (.D(undriven_2), .Q(register_8_q), .clk(clock_1_out), .clr(and_8_out));  // open: en
  Register register_9 (.D(undriven_2), .en(clock_1_out), .clr(and_9_out));  // open: Q, clk
  Register register_10 (.D(undriven_2), .clk(clock_1_out), .clr(and_10_out));  // open: en, Q
  Register register_11 (.D(undriven_2), .clk(clock_1_out), .clr(and_11_out));  // open: en, Q
  Register register_12 (.D(undriven_2), .clk(clock_1_out), .clr(and_12_out));  // open: en, Q
  Register register_13 (.D(undriven_2), .clk(clock_1_out), .clr(and_13_out));  // open: en, Q
  Register register_14 (.D(undriven_2), .clk(clock_1_out), .clr(and_14_out));  // open: en, Q
  Register register_15 (.D(undriven_2), .clk(clock_1_out), .clr(and_15_out));  // open: en, Q
  Register register_16 (.D(undriven_2), .clk(clock_1_out), .clr(and_16_out));  // open: en, Q
  Multiplexer #(.select(3), .width(8)) multiplexer_1 (
    .in0(register_1_q), .in1(register_2_q), .in2(register_3_q), .in3(register_4_q), .in4(register_5_q),
    .in5(register_6_q), .in6(register_7_q), .in7(register_8_q), .out(multiplexer_1_out), .sel(in_1));  // open: en
  Multiplexer #(.select(3), .width(8)) multiplexer_2 (
    .in0(register_1_q), .in1(register_2_q), .in2(register_3_q), .in3(register_4_q), .in4(register_5_q),
    .in5(register_6_q), .in6(register_7_q), .in7(register_8_q), .out(multiplexer_2_out), .sel(in_2));  // open: en
endmodule
