// Logisim project 8-bit_2-address-indirect addressing mode.circ as structural Verilog: 5 circuits, main circuit main
// 16
module main (
  input  [7:0] PC_IN,
  input  RESET,
  input  [7:0] DATA_IN,
  input  [7:0] DATA_IN_2,
  output [15:0] out_5,
  output [7:0] COUNTER
);

  wire clock_1_out, not_1_out, not_2_out, PC_SHIFT_out;
  wire [3:0] IR_q_2, IR_q_3;
  wire [7:0] IR_q, MAR_q, pc_1_output, RA_q, ram_2_data, RB_q, register_16_bit_1_dataout;
  wire [15:0] MBR_q, ram_1_data;
  wire [15:8] RZ_q;

  Clock clock_1 (.out(clock_1_out));
  Shift_Register #(.length(5)) PC_SHIFT (
    .in(PC_SHIFT_out), .clk(clock_1_out), .out(PC_SHIFT_out));  // open: shift, load, clr, d0, q0, d1, q1, d2, q2, d3, q3, d4, q4
  PC pc_1 (.Input(PC_IN), .PC_Enable(PC_SHIFT_out), .Clock(clock_1_out), .Reset(RESET), .Output(pc_1_output));
  COUNTER counter_1 (.R_W(RESET), .Clock(clock_1_out), .Output(COUNTER));  // open: Data_in
  Register MAR (.D(pc_1_output), .Q(MAR_q), .clk(clock_1_out), .clr(RESET));  // open: en
  not not_1 (not_1_out, PC_SHIFT_out);
  RAM #(.dataWidth(16)) ram_1 (.addr(MAR_q), .data(ram_1_data));  // open: sel, clk, ld, clr
  not not_2 (not_2_out, not_1_out);
  Register #(.width(16)) MBR (.D(ram_1_data), .Q(MBR_q), .clk(clock_1_out), .clr(RESET));  // open: en
  Register_16_Bit register_16_bit_1 (
    .DATAIN(DATA_IN), .Clock(clock_1_out), .Rx(IR_q_2), .DataOut(register_16_bit_1_dataout));  // open: R_prime_W
  Register #(.width(16)) IR (.D(MBR_q), .Q({IR_q_3, IR_q_2, IR_q}), .clk(clock_1_out), .clr(RESET));  // open: en
  RAM #(.bus("separate")) ram_2 (
    .addr(IR_q), .din(DATA_IN_2), .data(ram_2_data), .str(not_2_out), .clk(clock_1_out), .ld(not_1_out));  // open: sel, clr
  Register RA (.D(register_16_bit_1_dataout), .Q(RA_q), .clk(clock_1_out), .clr(RESET));  // open: en
  Register RB (.D(ram_2_data), .Q(RB_q), .clk(clock_1_out), .clr(RESET));  // open: en
  ALU_16_Bit_Ord alu_16_bit_ord_1 (.A(RA_q), .B(RB_q), .Opcode(IR_q_3), .DataOut(out_5));  // open: Shifter_Rotator
  Register #(.width(16)) RZ (.D(out_5), .Q({RZ_q, DATA_IN}), .clk(clock_1_out), .clr(RESET));  // open: en
  Hex_Digit_Display hex_digit_display_1 (.value(out_5[15:12]));  // open: dp
  Hex_Digit_Display hex_digit_display_2 (.value(out_5[11:8]));  // open: dp
  Hex_Digit_Display hex_digit_display_3 (.value(out_5[7:4]));  // open: dp
  Hex_Digit_Display hex_digit_display_4 (.value(out_5[3:0]));  // open: dp

  // Notes on the sheet:
  //   CODE MEMORY
endmodule

// Rx
module Register_16_Bit (
  input  [7:0] DATAIN,
  input  Clock,
  input  R_prime_W,
  input  [3:0] Rx,
  output [7:0] DataOut
);

  wire decoder_1_out0, decoder_1_out1, decoder_1_out2, decoder_1_out3, decoder_1_out4, decoder_1_out5,
       decoder_1_out6, decoder_1_out7, decoder_1_out8, decoder_1_out9, decoder_1_out10, decoder_1_out11,
       decoder_1_out12, decoder_1_out13, decoder_1_out14, decoder_1_out15, not_1_out;
  wire [3:0] undriven, undriven_2;
  wire [7:0] R0_q, R1_q, R2_q, R3_q, R4_q, R5_q, R6_q, R7_q, R8_q, R9_q, R10_q, R11_q, R12_q, R13_q, R14_q,
       R15_q;

  not not_1 (not_1_out, R_prime_W);
  Hex_Digit_Display hex_digit_display_1 (.value(undriven));  // open: dp
  Hex_Digit_Display hex_digit_display_2 (.value(undriven_2));  // open: dp
  Hex_Digit_Display hex_digit_display_3 (.value(DATAIN[3:0]));  // open: dp
  Hex_Digit_Display hex_digit_display_4 (.value(DATAIN[7:4]));  // open: dp
  Decoder #(.select(4), .disabled(0)) decoder_1 (
    .out0(decoder_1_out0), .out1(decoder_1_out1), .out2(decoder_1_out2), .out3(decoder_1_out3),
    .out4(decoder_1_out4), .out5(decoder_1_out5), .out6(decoder_1_out6), .out7(decoder_1_out7),
    .out8(decoder_1_out8), .out9(decoder_1_out9), .out10(decoder_1_out10), .out11(decoder_1_out11),
    .out12(decoder_1_out12), .out13(decoder_1_out13), .out14(decoder_1_out14), .out15(decoder_1_out15),
    .sel(Rx), .en(not_1_out));
  Register R0 (.D(DATAIN), .en(decoder_1_out0), .Q(R0_q), .clk(Clock));  // open: clr
  Register R1 (.D(DATAIN), .en(decoder_1_out1), .Q(R1_q), .clk(Clock));  // open: clr
  Register R2 (.D(DATAIN), .en(decoder_1_out2), .Q(R2_q), .clk(Clock));  // open: clr
  Register R3 (.D(DATAIN), .en(decoder_1_out3), .Q(R3_q), .clk(Clock));  // open: clr
  Register R4 (.D(DATAIN), .en(decoder_1_out4), .Q(R4_q), .clk(Clock));  // open: clr
  Register R5 (.D(DATAIN), .en(decoder_1_out5), .Q(R5_q), .clk(Clock));  // open: clr
  Register R6 (.D(DATAIN), .en(decoder_1_out6), .Q(R6_q), .clk(Clock));  // open: clr
  Register R7 (.D(DATAIN), .en(decoder_1_out7), .Q(R7_q), .clk(Clock));  // open: clr
  Register R8 (.en(decoder_1_out8), .Q(R8_q), .clk(Clock));  // open: D, clr
  Register R9 (.D(DATAIN), .en(decoder_1_out9), .Q(R9_q), .clk(Clock));  // open: clr
  Register R10 (.D(DATAIN), .en(decoder_1_out10), .Q(R10_q), .clk(Clock));  // open: clr
  Register R11 (.D(DATAIN), .en(decoder_1_out11), .Q(R11_q), .clk(Clock));  // open: clr
  Register R12 (.D(DATAIN), .en(decoder_1_out12), .Q(R12_q), .clk(Clock));  // open: clr
  Register R13 (.D(DATAIN), .en(decoder_1_out13), .Q(R13_q), .clk(Clock));  // open: clr
  Register R14 (.D(DATAIN), .en(decoder_1_out14), .Q(R14_q), .clk(Clock));  // open: clr
  Register R15 (.D(DATAIN), .en(decoder_1_out15), .Q(R15_q), .clk(Clock));  // open: clr
  Multiplexer #(.select(4), .width(8), .disabled(0)) multiplexer_1 (
    .in0(R0_q), .in1(R1_q), .in2(R2_q), .in3(R3_q), .in4(R4_q), .in5(R5_q), .in6(R6_q), .in7(R7_q),
    .in8(R8_q), .in9(R9_q), .in10(R10_q), .in11(R11_q), .in12(R12_q), .in13(R13_q), .in14(R14_q),
    .in15(R15_q), .out(DataOut), .sel(Rx), .en(R_prime_W));
  Hex_Digit_Display hex_digit_display_5 (.value(DataOut[7:4]));  // open: dp
  Hex_Digit_Display hex_digit_display_6 (.value(DataOut[3:0]));  // open: dp
endmodule

// ALU
module ALU_16_Bit_Ord (
  input  [7:0] A,
  input  [7:0] B,
  input  [3:0] Opcode,
  input  [15:0] Shifter_Rotator,
  output [15:0] DataOut
);

  wire adder_1_cout, subtractor_1_bout;
  wire [7:0] adder_1_out, and_1_out, bit_extender_1_out, bit_extender_2_out, divider_1_out, divider_1_rem,
       multiplier_1_cout, multiplier_1_out, or_1_out, subtractor_1_out;
  wire [15:0] adder_2_out, not_1_out, shifter_1_out, shifter_2_out, shifter_3_out, shifter_4_out,
       subtractor_2_out;

  Hex_Digit_Display hex_digit_display_1 (.value(A[3:0]));  // open: dp
  Hex_Digit_Display hex_digit_display_2 (.value(A[7:4]));  // open: dp
  Hex_Digit_Display hex_digit_display_3 (.value(B[7:4]));  // open: dp
  Hex_Digit_Display hex_digit_display_4 (.value(B[3:0]));  // open: dp
  Adder adder_1 (.a(A), .b(B), .out(adder_1_out), .cout(adder_1_cout));  // open: cin
  assign bit_extender_1_out = {{7{1'b0}}, adder_1_cout};  // Bit_Extender bit_extender_1
  Subtractor subtractor_1 (.a(A), .b(B), .out(subtractor_1_out), .bout(subtractor_1_bout));  // open: bin
  assign bit_extender_2_out = {{7{1'b0}}, subtractor_1_bout};  // Bit_Extender bit_extender_2
  Multiplier multiplier_1 (.a(A), .b(B), .out(multiplier_1_out), .cout(multiplier_1_cout));  // open: cin
  Divider divider_1 (.a(A), .b(B), .out(divider_1_out), .rem(divider_1_rem));  // open: upper
  Adder #(.width(16)) adder_2 (.a({B, A}), .b(16'h1), .out(adder_2_out));  // open: cin, cout
  Subtractor #(.width(16)) subtractor_2 (.a({B, A}), .b(16'h1), .out(subtractor_2_out));  // open: bin, bout
  assign and_1_out = A & B;  // AND_Gate and_1, 8 bits wide
  assign or_1_out = A | B;  // OR_Gate or_1, 8 bits wide
  assign not_1_out = ~{B, A};  // NOT_Gate not_1, 16 bits wide
  Shifter #(.width(16), .shift("lr")) shifter_1 (.in({B, A}), .\dist (Shifter_Rotator[3:0]), .out(shifter_1_out));
  Shifter #(.width(16)) shifter_2 (.in({B, A}), .\dist (Shifter_Rotator[7:4]), .out(shifter_2_out));
  Shifter #(.width(16), .shift("rr")) shifter_3 (.in({B, A}), .\dist (Shifter_Rotator[11:8]), .out(shifter_3_out));
  Shifter #(.width(16), .shift("rl")) shifter_4 (.in({B, A}), .\dist (Shifter_Rotator[15:12]), .out(shifter_4_out));
  Multiplexer #(.select(4), .width(16)) multiplexer_1 (
    .in0({B, A}), .in1({B, A}), .in2({bit_extender_1_out, adder_1_out}),
    .in3({bit_extender_2_out, subtractor_1_out}), .in4({multiplier_1_cout, multiplier_1_out}),
    .in5({divider_1_rem, divider_1_out}), .in6(adder_2_out), .in7(subtractor_2_out),
    .in8({{8{1'b0}}, and_1_out}), .in9({{8{1'b0}}, or_1_out}), .in10(not_1_out), .in11({A, B}),
    .in12(shifter_1_out), .in13(shifter_2_out), .in14(shifter_3_out), .in15(shifter_4_out), .out(DataOut),
    .sel(Opcode));  // open: en
  Hex_Digit_Display hex_digit_display_5 (.value(DataOut[15:12]));  // open: dp
  Hex_Digit_Display hex_digit_display_6 (.value(DataOut[11:8]));  // open: dp
  Hex_Digit_Display hex_digit_display_7 (.value(DataOut[3:0]));  // open: dp
  Hex_Digit_Display hex_digit_display_8 (.value(DataOut[7:4]));  // open: dp
endmodule

module PC (
  input  [7:0] Input,
  input  PC_Enable,
  input  Clock,
  input  Reset,
  output [7:0] Output
);

  wire [7:0] adder_1_out;

  Adder adder_1 (.a(Input), .b(Output), .out(adder_1_out), .cin(1'b1));  // open: cout
  Hex_Digit_Display hex_digit_display_1 (.value(Output[7:4]));  // open: dp
  Counter counter_1 (.D(adder_1_out), .count(PC_Enable), .Q(Output), .clk(Clock), .clr(Reset));  // open: load, carry
  Hex_Digit_Display hex_digit_display_2 (.value(Output[3:0]));  // open: dp
endmodule

module COUNTER (
  input  R_W,
  input  [7:0] Data_in,
  input  Clock,
  output [7:0] Output
);

  wire not_1_out;

  not not_1 (not_1_out, R_W);
  Counter counter_1 (.load(R_W), .D(Data_in), .count(not_1_out), .Q(Output), .clk(Clock));  // open: carry, clr
endmodule
