// Logisim project 8bit 1 add format immediate addressing mode [2].circ as structural Verilog: 5 circuits, main circuit main
module main (
  input  [7:0] in_1,
  input  [2:0] in_2,
  output [15:0] out_3
);

  wire CLOCK, nor_1_out, not_1_out, not_2_out, reset, shift_register_1_out;
  wire [7:0] bit_extender_1_out, bit_extender_2_out, IR_q, MAR_q, MBR_q, pc_1_pc_out, RA_CONTENTS, RA_q,
       rom_1_data;
  wire [15:0] ACC_CONTENTS, multiplexer_1_out;

  Shift_Register #(.length(4)) shift_register_1 (
    .in(shift_register_1_out), .clk(CLOCK), .out(shift_register_1_out));  // open: shift, load, clr, d0, q0, d1, q1, d2, q2, d3, q3
  pc pc_1 (.PC_INput(in_1), .pc__enable(shift_register_1_out), .clock(CLOCK), .PC_OUT(pc_1_pc_out), .PC_reset(reset));
  Register MAR (.D(pc_1_pc_out), .Q(MAR_q), .clk(CLOCK), .clr(reset));  // open: en
  Button button_1 (.out(reset));
  ROM rom_1 (.addr(MAR_q), .data(rom_1_data));  // open: sel
  Register MBR (.D(rom_1_data), .Q(MBR_q), .clk(CLOCK), .clr(reset));  // open: en
  Clock clock_1 (.out(CLOCK));
  Register IR (.D(MBR_q), .Q(IR_q), .clk(CLOCK), .clr(reset));  // open: en
  not not_1 (not_1_out, nor_1_out);
  Hex_Digit_Display hex_digit_display_1 (.value(RA_CONTENTS[7:4]));  // open: dp
  register_files register_files_1 (
    .clock(CLOCK), .DATA_IN(bit_extender_2_out), .R_W(not_1_out), .S(IR_q[3:0]), .DATA_OUT(RA_CONTENTS));
  not not_2 (not_2_out, IR_q[4]);
  nor nor_1 (nor_1_out, IR_q[7], IR_q[6], IR_q[5], not_2_out);
  Hex_Digit_Display hex_digit_display_2 (.value(RA_CONTENTS[3:0]));  // open: dp
  Register RA (.D(RA_CONTENTS), .Q(RA_q), .clk(CLOCK), .clr(reset));  // open: en
  alu alu_1 (.Acc(bit_extender_1_out), .b(RA_q), .shift_op(in_2), .s(IR_q[7:4]), .\output (out_3));
  Hex_Digit_Display hex_digit_display_3 (.value(ACC_CONTENTS[11:8]));  // open: dp
  Hex_Digit_Display hex_digit_display_4 (.value(ACC_CONTENTS[15:12]));  // open: dp
  Register #(.width(16)) ACCUMLATOR (.D(out_3), .Q(ACC_CONTENTS), .clk(shift_register_1_out), .clr(reset));  // open: en
  Hex_Digit_Display hex_digit_display_5 (.value(ACC_CONTENTS[3:0]));  // open: dp
  Hex_Digit_Display hex_digit_display_6 (.value(ACC_CONTENTS[7:4]));  // open: dp
  Bit_Extender #(.in_width(16), .out_width(8)) bit_extender_1 (.in(ACC_CONTENTS), .out(bit_extender_1_out));
  Multiplexer #(.width(16), .enable("false")) multiplexer_1 (
    .in0(ACC_CONTENTS), .out(multiplexer_1_out), .sel(not_1_out));  // open: in1
  Bit_Extender #(.in_width(16), .out_width(8)) bit_extender_2 (.in(multiplexer_1_out), .out(bit_extender_2_out));

  // Notes on the sheet:
  //   contents of rom_1 (hex, n*v repeats v):
  //   51 31
endmodule

// RF
module register_files (
  input  clock,
  input  [7:0] DATA_IN,
  input  R_W,
  input  [3:0] S,
  output [7:0] DATA_OUT
);

  wire decoder_1_out0, decoder_1_out1, decoder_1_out2, decoder_1_out3, decoder_1_out4, decoder_1_out5,
       decoder_1_out6, decoder_1_out7, decoder_1_out8, decoder_1_out9, decoder_1_out10, decoder_1_out11,
       decoder_1_out12, decoder_1_out13, decoder_1_out14, decoder_1_out15, not_1_out;
  wire [7:0] R0_q, R1_q, R2_q, R3_q, R4_q, R5_q, R6_q, R7_q, R8_q, R9_q, R10_q, R11_q, R12_q, R13_q, R14_q,
       R15_q;

  Hex_Digit_Display hex_digit_display_1 (.value(DATA_IN[7:4]));  // open: dp
  not not_1 (not_1_out, R_W);
  Decoder #(.select(4), .disabled(0)) decoder_1 (
    .out0(decoder_1_out0), .out1(decoder_1_out1), .out2(decoder_1_out2), .out3(decoder_1_out3),
    .out4(decoder_1_out4), .out5(decoder_1_out5), .out6(decoder_1_out6), .out7(decoder_1_out7),
    .out8(decoder_1_out8), .out9(decoder_1_out9), .out10(decoder_1_out10), .out11(decoder_1_out11),
    .out12(decoder_1_out12), .out13(decoder_1_out13), .out14(decoder_1_out14), .out15(decoder_1_out15),
    .sel(S), .en(not_1_out));
  Hex_Digit_Display hex_digit_display_2 (.value(DATA_IN[3:0]));  // open: dp
  Register R0 (.D(DATA_IN), .en(decoder_1_out0), .Q(R0_q), .clk(clock));  // open: clr
  Register R1 (.D(DATA_IN), .en(decoder_1_out1), .Q(R1_q), .clk(clock));  // open: clr
  Register R2 (.D(DATA_IN), .en(decoder_1_out2), .Q(R2_q), .clk(clock));  // open: clr
  Register R3 (.D(DATA_IN), .en(decoder_1_out3), .Q(R3_q), .clk(clock));  // open: clr
  Register R4 (.D(DATA_IN), .en(decoder_1_out4), .Q(R4_q), .clk(clock));  // open: clr
  Register R5 (.D(DATA_IN), .en(decoder_1_out5), .Q(R5_q), .clk(clock));  // open: clr
  Register R6 (.D(DATA_IN), .en(decoder_1_out6), .Q(R6_q), .clk(clock));  // open: clr
  Register R7 (.D(DATA_IN), .en(decoder_1_out7), .Q(R7_q), .clk(clock));  // open: clr
  Register R8 (.D(DATA_IN), .en(decoder_1_out8), .Q(R8_q));  // open: clk, clr
  Register R9 (.D(DATA_IN), .en(decoder_1_out9), .Q(R9_q), .clk(clock));  // open: clr
  Register R10 (.D(DATA_IN), .en(decoder_1_out10), .Q(R10_q), .clk(clock));  // open: clr
  Register R11 (.D(DATA_IN), .en(decoder_1_out11), .Q(R11_q), .clk(clock));  // open: clr
  Register R12 (.D(DATA_IN), .en(decoder_1_out12), .Q(R12_q), .clk(clock));  // open: clr
  Register R13 (.D(DATA_IN), .en(decoder_1_out13), .Q(R13_q), .clk(clock));  // open: clr
  Register R14 (.D(DATA_IN), .en(decoder_1_out14), .Q(R14_q), .clk(clock));  // open: clr
  Register R15 (.D(DATA_IN), .en(decoder_1_out15), .Q(R15_q), .clk(clock));  // open: clr
  Multiplexer #(.select(4), .width(8)) multiplexer_1 (
    .in0(R0_q), .in1(R1_q), .in2(R2_q), .in3(R3_q), .in4(R4_q), .in5(R5_q), .in6(R6_q), .in7(R7_q),
    .in8(R8_q), .in9(R9_q), .in10(R10_q), .in11(R11_q), .in12(R12_q), .in13(R13_q), .in14(R14_q),
    .in15(R15_q), .out(DATA_OUT), .sel(S), .en(R_W));
  Hex_Digit_Display hex_digit_display_3 (.value(DATA_OUT[7:4]));  // open: dp
  Hex_Digit_Display hex_digit_display_4 (.value(DATA_OUT[3:0]));  // open: dp
endmodule

// ALU
module alu (
  input  [7:0] Acc,
  input  [7:0] b,
  input  [3:0] s,
  input  [2:0] shift_op,
  output [15:0] \output 
);

  wire adder_1_cout, adder_2_cout, subtractor_1_bout, subtractor_2_bout;
  wire [7:0] adder_1_out, adder_2_out, and_1_out, bit_extender_1_out, bit_extender_2_out, bit_extender_3_out,
       bit_extender_4_out, divider_1_out, divider_1_rem, multiplier_1_cout, multiplier_1_out, not_1_out,
       or_1_out, shifter_1_out, shifter_2_out, shifter_3_out, shifter_4_out, subtractor_1_out,
       subtractor_2_out;
  wire [15:0] bit_extender_5_out, bit_extender_6_out, bit_extender_7_out, bit_extender_8_out,
       bit_extender_9_out, bit_extender_10_out, bit_extender_11_out;

  Subtractor subtractor_1 (.a(b), .b(8'h1), .out(subtractor_1_out), .bout(subtractor_1_bout));  // open: bin
  Adder adder_1 (.a(Acc), .b(Acc), .out(adder_1_out), .cout(adder_1_cout));  // open: cin
  Subtractor subtractor_2 (.a(Acc), .b(b), .out(subtractor_2_out), .bout(subtractor_2_bout));  // open: bin
  Multiplier multiplier_1 (.a(Acc), .b(b), .out(multiplier_1_out), .cout(multiplier_1_cout));  // open: cin
  Divider divider_1 (.a(Acc), .b(b), .out(divider_1_out), .rem(divider_1_rem));  // open: upper
  Adder adder_2 (.a(b), .b(8'h1), .out(adder_2_out), .cout(adder_2_cout));  // open: cin
  assign and_1_out = Acc & b;  // AND_Gate and_1, 8 bits wide
  assign or_1_out = Acc | b;  // OR_Gate or_1, 8 bits wide
  assign not_1_out = ~b;  // NOT_Gate not_1, 8 bits wide
  assign bit_extender_1_out = {{7{1'b0}}, adder_1_cout};  // Bit_Extender bit_extender_1
  assign bit_extender_2_out = {{7{1'b0}}, subtractor_2_bout};  // Bit_Extender bit_extender_2
  assign bit_extender_3_out = {{7{1'b0}}, adder_2_cout};  // Bit_Extender bit_extender_3
  assign bit_extender_4_out = {{7{1'b0}}, subtractor_1_bout};  // Bit_Extender bit_extender_4
  assign bit_extender_5_out = {{8{1'b0}}, not_1_out};  // Bit_Extender bit_extender_5
  Shifter #(.shift("lr")) shifter_1 (.in(b), .\dist (shift_op), .out(shifter_1_out));
  Shifter shifter_2 (.in(b), .\dist (shift_op), .out(shifter_2_out));
  Shifter #(.shift("rr")) shifter_3 (.in(b), .\dist (shift_op), .out(shifter_3_out));
  Shifter #(.shift("rl")) shifter_4 (.in(b), .\dist (shift_op), .out(shifter_4_out));
  assign bit_extender_6_out = {{8{1'b0}}, b};  // Bit_Extender bit_extender_6
  assign bit_extender_7_out = {{8{1'b0}}, shifter_1_out};  // Bit_Extender bit_extender_7
  assign bit_extender_8_out = {{8{1'b0}}, shifter_2_out};  // Bit_Extender bit_extender_8
  assign bit_extender_9_out = {{8{1'b0}}, shifter_3_out};  // Bit_Extender bit_extender_9
  assign bit_extender_10_out = {{8{1'b0}}, shifter_4_out};  // Bit_Extender bit_extender_10
  assign bit_extender_11_out = {{8{1'b0}}, Acc};  // Bit_Extender bit_extender_11
  Multiplexer #(.select(4), .width(16), .enable("false")) multiplexer_1 (
    .in0(bit_extender_6_out), .in1(bit_extender_11_out), .in2({bit_extender_1_out, adder_1_out}),
    .in3({bit_extender_2_out, subtractor_2_out}), .in4({multiplier_1_cout, multiplier_1_out}),
    .in5({divider_1_rem, divider_1_out}), .in6({bit_extender_3_out, adder_2_out}),
    .in7({bit_extender_4_out, subtractor_1_out}), .in8({{8{1'b0}}, and_1_out}), .in9({{8{1'b0}}, or_1_out}),
    .in10(bit_extender_5_out), .in11({Acc, b}), .in12(bit_extender_7_out), .in13(bit_extender_8_out),
    .in14(bit_extender_9_out), .in15(bit_extender_10_out), .out(\output ), .sel(s));
endmodule

// PC
module pc (
  input  [7:0] PC_INput,
  input  pc__enable,
  input  PC_reset,
  input  clock,
  output [7:0] PC_OUT
);

  wire [7:0] adder_1_out;

  Hex_Digit_Display hex_digit_display_1 (.value(PC_INput[3:0]));  // open: dp
  Hex_Digit_Display hex_digit_display_2 (.value(PC_INput[7:4]));  // open: dp
  Adder adder_1 (.a(PC_INput), .b(PC_OUT), .out(adder_1_out), .cin(1'b1));  // open: cout
  Hex_Digit_Display hex_digit_display_3 (.value(PC_OUT[7:4]));  // open: dp
  Register register_1 (.D(adder_1_out), .en(pc__enable), .Q(PC_OUT), .clk(clock), .clr(PC_reset));
  Hex_Digit_Display hex_digit_display_4 (.value(PC_OUT[3:0]));  // open: dp
endmodule

module \xor  (
  input  [3:0] opcode,
  output o
);

  wire not_1_out, not_2_out, not_3_out;

  not not_1 (not_1_out, opcode[3]);
  not not_2 (not_2_out, opcode[1]);
  not not_3 (not_3_out, opcode[0]);
  nor nor_1 (o, not_1_out, opcode[2], not_2_out, not_3_out);
endmodule
