// Logisim project 8bit 2 add format register indirect MISD.circ as structural Verilog
module main (
);


  // Notes on the sheet:
  //   COA PROJECT
  //   Team details
  //   Veerraj. S. Chitragar 427
  //   Avinash Nayak 431
  //   Yallava Pujar 424
  //   Sujal K 411
  //   GUIDANCE : 
  //   NAMRATHA HIREMATH
endmodule

module all (
  input  [11:0] in_1,
  output [11:0] out_2,
  output [7:0] out_3,
  output [7:0] out_4,
  output [15:0] out_5,
  output out_6,
  output out_7,
  output out_8,
  output out_9,
  output out_10,
  output out_11,
  output out_12,
  output out_13,
  output [11:0] out_14
);

  wire Clock, Reset;
  wire [15:0] out02;
  wire [15:12] CM_out;

  allintegration allintegration_1 (
    .PC_input(in_1), .PC_OUTPUT(out_14), .CM_OUTPUT({CM_out, out_2}), .Register_out(out_3), .Clock(Clock),
    .Reset(Reset), .Zero(out_13), .Positive(out_7), .Negative(out_8), .Carry(out_12), .Half_carry(out_9),
    .Even(out_10), .Odd(out_11), .Overflow(out_6), .ALU_output(out_5), .Mem_output(out_4), .Out_02(out02));
  Button button_1 (.out(Clock));
  Hex_Digit_Display hex_digit_display_1 (.value(in_1[7:4]));  // open: dp
  Hex_Digit_Display hex_digit_display_2 (.value(in_1[11:8]));  // open: dp
  Button button_2 (.out(Reset));
  Hex_Digit_Display hex_digit_display_3 (.value(out_3[3:0]));  // open: dp
  Hex_Digit_Display hex_digit_display_4 (.value(out_3[7:4]));  // open: dp
  Hex_Digit_Display hex_digit_display_5 (.value(in_1[3:0]));  // open: dp
  Hex_Digit_Display hex_digit_display_6 (.value(out_14[11:8]));  // open: dp
  Hex_Digit_Display hex_digit_display_7 (.value(out_2[7:4]));  // open: dp
  Hex_Digit_Display hex_digit_display_8 (.value(out_2[11:8]));  // open: dp
  Hex_Digit_Display hex_digit_display_9 (.value(out_4[7:4]));  // open: dp
  Hex_Digit_Display hex_digit_display_10 (.value(out_14[3:0]));  // open: dp
  Hex_Digit_Display hex_digit_display_11 (.value(out_14[7:4]));  // open: dp
  Hex_Digit_Display hex_digit_display_12 (.value(out_2[3:0]));  // open: dp
  Hex_Digit_Display hex_digit_display_13 (.value(out_4[3:0]));  // open: dp
  Hex_Digit_Display hex_digit_display_14 (.value(out_5[11:8]));  // open: dp
  Hex_Digit_Display hex_digit_display_15 (.value(out_5[15:12]));  // open: dp
  Hex_Digit_Display hex_digit_display_16 (.value(out_5[7:4]));  // open: dp
  Hex_Digit_Display hex_digit_display_17 (.value(out_5[3:0]));  // open: dp
  // Pins of 12 and 16 bits meet at {CM_out, out_2}

  // Other names for the same wires on the sheet: _1st_input[7:0] = out_3; _2ind_input[7:0] = out_4;
  //   ALU_output[15:0] = out_5; Carry = out_12; CM_out[11:0] = out_2; Even = out_10; Half_carry = out_9;
  //   Negative = out_8; Odd = out_11; Overflow = out_6; PC_input[11:0] = in_1; PC_out[11:0] = out_14;
  //   Positive = out_7; Zero = out_13

  // Notes on the sheet:
  //   Main
  //   PSW
  //   =
endmodule

module allintegration (
  input  [11:0] PC_input,
  input  Clock,
  input  Reset,
  output [7:0] Register_out,
  output [15:0] ALU_output,
  output [11:0] PC_OUTPUT,
  output [15:0] CM_OUTPUT,
  output [7:0] Mem_output,
  output [15:0] Out_02,
  output Zero,
  output Positive,
  output Negative,
  output Carry,
  output Half_carry,
  output Even,
  output Odd,
  output Overflow
);

  wire not_1_out, PC_shift_out, selector_1_output, selector_2_output;
  wire [3:0] IR_q_2, MAR_q, MAR_q_2, MAR_q_3;
  wire [7:0] ALU_exchange, ALU_exchange_2, multiplexer_1_out, multiplexer_2_out, or_1_out, or_1_out_2,
       or_2_out, or_2_out_2, RA_q, RB_q, register_1_regi_out_02;
  wire [15:0] ALU_aluoutput, ALU_register, ALU_store, bit_extender_1_out, bit_extender_2_out, IR_q, MBR_q;

  Hex_Digit_Display hex_digit_display_1 (.value(PC_input[11:8]));  // open: dp
  Hex_Digit_Display hex_digit_display_2 (.value(PC_input[7:4]));  // open: dp
  Hex_Digit_Display hex_digit_display_3 (.value(PC_input[3:0]));  // open: dp
  Hex_Digit_Display hex_digit_display_4 (.value(MAR_q_3));  // open: dp
  Program_counter program_counter_1 (
    .PC_INput(PC_input), .PC_enable(PC_shift_out), .Clock(Clock), .PC_reset(Reset), .PC_OUT(PC_OUTPUT));
  Shift_Register #(.length(5)) PC_shift (
    .in(PC_shift_out), .clk(Clock), .out(PC_shift_out));  // open: shift, load, clr, d0, q0, d1, q1, d2, q2, d3, q3, d4, q4
  Hex_Digit_Display hex_digit_display_5 (.value(MAR_q));  // open: dp
  Hex_Digit_Display hex_digit_display_6 (.value(MAR_q_2));  // open: dp
  Register_part #(.width(12)) MAR (.D(PC_OUTPUT), .en(Clock), .Q({MAR_q_3, MAR_q_2, MAR_q}), .clk(Clock), .clr(Reset));
  not not_1 (not_1_out, PC_shift_out);
  ROM #(.addrWidth(12), .dataWidth(16)) rom_1 (.addr({MAR_q_3, MAR_q_2, MAR_q}), .data(CM_OUTPUT));  // open: sel
  Multiplexer #(.width(8)) multiplexer_1 (
    .in0(RA_q), .in1(or_1_out), .out(multiplexer_1_out), .sel(selector_1_output));  // open: en
  Register_part #(.width(16)) MBR (.D(CM_OUTPUT), .Q(MBR_q), .clk(Clock), .clr(Reset));  // open: en
  Hex_Digit_Display hex_digit_display_7 (.value(Mem_output[7:4]));  // open: dp
  selector selector_1 (.Input({or_1_out_2, or_1_out}), .Output(selector_1_output));
  Register_part #(.width(16)) IR (
    .D(MBR_q), .Q({IR_q[15:12], IR_q_2, IR_q[7:0]}), .clk(Clock), .clr(Reset));  // open: en
  RAM #(.bus("separate")) ram_1 (
    .addr(register_1_regi_out_02), .din(multiplexer_2_out), .data(Mem_output), .str(not_1_out), .clk(Clock),
    .ld(not_1_out));  // open: sel, clr
  Hex_Digit_Display hex_digit_display_8 (.value(Mem_output[3:0]));  // open: dp
  Hex_Digit_Display hex_digit_display_9 (.value(Register_out[7:4]));  // open: dp
  Hex_Digit_Display hex_digit_display_10 (.value(Register_out[3:0]));  // open: dp
  assign {or_1_out_2, or_1_out} = bit_extender_1_out | ALU_register;  // OR_Gate or_1, 16 bits wide
  Register register_1 (
    .Data_in(multiplexer_1_out), .R_W(not_1_out), .input01(IR_q[7:4]), .Input_02(IR_q[3:0]), .Clock(Clock),
    .Regi_out_01(Register_out), .Regi_out_02(register_1_regi_out_02));
  selector selector_2 (.Input({or_2_out_2, or_2_out}), .Output(selector_2_output));
  Multiplexer #(.width(8)) multiplexer_2 (
    .in0(RB_q), .in1(or_2_out), .out(multiplexer_2_out), .sel(selector_2_output));  // open: en
  Register_part RA (.D(Register_out), .Q(RA_q), .clk(Clock), .clr(Reset));  // open: en
  assign {or_2_out_2, or_2_out} = bit_extender_2_out | ALU_store;  // OR_Gate or_2, 16 bits wide
  Hex_Digit_Display hex_digit_display_11 (.value(ALU_output[11:8]));  // open: dp
  Hex_Digit_Display hex_digit_display_12 (.value(ALU_output[15:12]));  // open: dp
  Register_part RB (.D(Mem_output), .Q(RB_q), .clk(Clock), .clr(Reset));  // open: en
  Hex_Digit_Display hex_digit_display_13 (.value(ALU_output[3:0]));  // open: dp
  Hex_Digit_Display hex_digit_display_14 (.value(ALU_output[7:4]));  // open: dp
  Register_part #(.width(16)) RZ (.D(ALU_aluoutput), .Q(ALU_output), .clk(Clock), .clr(Reset));  // open: en
  assign bit_extender_1_out = {{8{1'b0}}, ALU_exchange};  // Bit_Extender bit_extender_1
  assign bit_extender_2_out = {{8{1'b0}}, ALU_exchange_2};  // Bit_Extender bit_extender_2
  ALU ALU (
    .A(RA_q), .B(RB_q), .SELECT_01(IR_q_2), .Exchange({ALU_exchange_2, ALU_exchange}),
    .SELECT_02(IR_q[15:12]), .ALUoutput(ALU_aluoutput), .Register(ALU_register), .ALUoutput02(Out_02),
    .Store(ALU_store), .Carry(Carry), .evenParity(Even), .OddPriority(Odd), .Overflow(Overflow),
    .Half_carry(Half_carry), .Zero_flag(Zero), .Negative(Negative), .positive(Positive));

  // Other names for the same wires on the sheet: Postive = Positive; Zero_flag = Zero

  // Notes on the sheet:
  //   PC
  //   01000
  //   Code Memory
  //   contents of rom_1 (hex, n*v repeats v):
  //   267 0 431 512 246
  //   PSW
  //   Register
endmodule

module ALU (
  input  [7:0] A,
  input  [7:0] B,
  input  [3:0] SELECT_01,
  input  [3:0] SELECT_02,
  output Carry,
  output [15:0] ALUoutput,
  output [15:0] Register,
  output [15:0] Exchange,
  output [15:0] Store,
  output [15:0] ALUoutput02,
  output evenParity,
  output OddPriority,
  output Overflow,
  output Half_carry,
  output Zero_flag,
  output Negative,
  output positive
);

  wire adder_1_cout, or_2_out, or_3_out, subtractor_1_bout;
  wire [2:0] bit_extender_2_out;
  wire [7:0] adder_1_out, adder_2_out, and_1_out, bit_extender_1_out, bit_extender_5_out, bit_extender_6_out,
       divider_1_out, divider_1_rem, multiplier_1_cout, multiplier_1_out, not_1_out, or_1_out, shifter_1_out,
       shifter_2_out, shifter_3_out, shifter_4_out, subtractor_1_out, subtractor_2_out;
  wire [15:0] bit_extender_3_out, bit_extender_4_out, bit_extender_7_out, bit_extender_8_out,
       bit_extender_9_out, bit_extender_10_out, bit_extender_11_out, bit_extender_12_out,
       bit_extender_13_out, bit_extender_14_out, bit_extender_15_out, demultiplexer_1_out0,
       demultiplexer_1_out2, demultiplexer_1_out3, demultiplexer_1_out4, demultiplexer_1_out5,
       demultiplexer_1_out6, demultiplexer_1_out7, demultiplexer_1_out8, demultiplexer_1_out9,
       demultiplexer_1_out10, demultiplexer_1_out12, demultiplexer_1_out13, demultiplexer_1_out14,
       demultiplexer_1_out15;

  Hex_Digit_Display hex_digit_display_1 (.value(A[3:0]));  // open: dp
  Hex_Digit_Display hex_digit_display_2 (.value(A[7:4]));  // open: dp
  Hex_Digit_Display hex_digit_display_3 (.value(B[3:0]));  // open: dp
  Hex_Digit_Display hex_digit_display_4 (.value(B[7:4]));  // open: dp
  assign bit_extender_1_out = {{7{1'b0}}, 1'b1};  // Bit_Extender bit_extender_1
  Bit_Extender #(.out_width(3)) bit_extender_2 (.in(B), .out(bit_extender_2_out));
  assign bit_extender_3_out = {{8{1'b0}}, B};  // Bit_Extender bit_extender_3
  assign bit_extender_4_out = {{8{1'b0}}, A};  // Bit_Extender bit_extender_4
  Adder adder_1 (.a(A), .b(B), .out(adder_1_out), .cout(adder_1_cout));  // open: cin
  Subtractor subtractor_1 (.a(A), .b(B), .out(subtractor_1_out), .bout(subtractor_1_bout));  // open: bin
  Multiplier multiplier_1 (.a(A), .b(B), .out(multiplier_1_out), .cout(multiplier_1_cout));  // open: cin
  Divider divider_1 (.a(A), .b(B), .out(divider_1_out), .rem(divider_1_rem));  // open: upper
  Adder adder_2 (.a(A), .b(bit_extender_1_out), .out(adder_2_out));  // open: cin, cout
  Subtractor subtractor_2 (.a(A), .b(bit_extender_1_out), .out(subtractor_2_out));  // open: bin, bout
  assign and_1_out = A & B;  // AND_Gate and_1, 8 bits wide
  assign or_1_out = A | B;  // OR_Gate or_1, 8 bits wide
  assign not_1_out = ~A;  // NOT_Gate not_1, 8 bits wide
  Shifter #(.shift("lr")) shifter_1 (.in(A), .\dist (bit_extender_2_out), .out(shifter_1_out));
  Shifter shifter_2 (.in(A), .\dist (bit_extender_2_out), .out(shifter_2_out));
  Shifter #(.shift("rr")) shifter_3 (.in(A), .\dist (bit_extender_2_out), .out(shifter_3_out));
  Shifter #(.shift("rl")) shifter_4 (.in(A), .\dist (bit_extender_2_out), .out(shifter_4_out));
  or or_2 (or_2_out, ALUoutput[15], ALUoutput[14], ALUoutput[13], ALUoutput[12], ALUoutput[11], ALUoutput[10], ALUoutput[9], ALUoutput[8], ALUoutput[7], ALUoutput[6], ALUoutput[5], ALUoutput[4], ALUoutput[3], ALUoutput[2], ALUoutput[1], ALUoutput[0]);
  not not_2 (Half_carry, or_2_out);
  not not_3 (positive, ALUoutput[15]);
  assign bit_extender_5_out = {{7{1'b0}}, adder_1_cout};  // Bit_Extender bit_extender_5
  assign bit_extender_6_out = {{7{1'b0}}, subtractor_1_bout};  // Bit_Extender bit_extender_6
  assign bit_extender_7_out = {{8{1'b0}}, adder_2_out};  // Bit_Extender bit_extender_7
  assign bit_extender_8_out = {{8{1'b0}}, subtractor_2_out};  // Bit_Extender bit_extender_8
  assign bit_extender_9_out = {{8{1'b0}}, and_1_out};  // Bit_Extender bit_extender_9
  assign bit_extender_10_out = {{8{1'b0}}, or_1_out};  // Bit_Extender bit_extender_10
  assign bit_extender_11_out = {{8{1'b0}}, not_1_out};  // Bit_Extender bit_extender_11
  assign bit_extender_12_out = {{8{1'b0}}, shifter_1_out};  // Bit_Extender bit_extender_12
  assign bit_extender_13_out = {{8{1'b0}}, shifter_2_out};  // Bit_Extender bit_extender_13
  assign bit_extender_14_out = {{8{1'b0}}, shifter_3_out};  // Bit_Extender bit_extender_14
  assign bit_extender_15_out = {{8{1'b0}}, shifter_4_out};  // Bit_Extender bit_extender_15
  or or_3 (or_3_out, ALUoutput[15], ALUoutput[14], ALUoutput[13], ALUoutput[12], ALUoutput[11], ALUoutput[10], ALUoutput[9], ALUoutput[8], ALUoutput[7], ALUoutput[6], ALUoutput[5], ALUoutput[4], ALUoutput[3], ALUoutput[2], ALUoutput[1], ALUoutput[0]);
  not not_4 (Zero_flag, or_3_out);
  or or_4 (Carry, adder_1_cout, subtractor_1_bout);
  and and_2 (Overflow, ALUoutput[15], ALUoutput[14], ALUoutput[13], ALUoutput[12], ALUoutput[11], ALUoutput[10], ALUoutput[9], ALUoutput[8], ALUoutput[7], ALUoutput[6], ALUoutput[5], ALUoutput[4], ALUoutput[3], ALUoutput[2], ALUoutput[1], ALUoutput[0]);
  Multiplexer #(.select(4), .width(16), .disabled(0)) multiplexer_1 (
    .in0(bit_extender_3_out), .in1(bit_extender_4_out), .in2({bit_extender_5_out, adder_1_out}),
    .in3({bit_extender_6_out, subtractor_1_out}), .in4({multiplier_1_cout, multiplier_1_out}),
    .in5({divider_1_rem, divider_1_out}), .in6(bit_extender_7_out), .in7(bit_extender_8_out),
    .in8(bit_extender_9_out), .in9(bit_extender_10_out), .in10(bit_extender_11_out), .in11({A, B}),
    .in12(bit_extender_12_out), .in13(bit_extender_13_out), .in14(bit_extender_14_out),
    .in15(bit_extender_15_out), .out(ALUoutput02), .sel(SELECT_02));  // open: en
  Hex_Digit_Display hex_digit_display_5 (.value(ALUoutput[11:8]));  // open: dp
  Hex_Digit_Display hex_digit_display_6 (.value(ALUoutput[15:12]));  // open: dp
  Multiplexer #(.select(4), .width(16), .disabled(0)) multiplexer_2 (
    .in0(bit_extender_3_out), .in1(bit_extender_4_out), .in2({bit_extender_5_out, adder_1_out}),
    .in3({bit_extender_6_out, subtractor_1_out}), .in4({multiplier_1_cout, multiplier_1_out}),
    .in5({divider_1_rem, divider_1_out}), .in6(bit_extender_7_out), .in7(bit_extender_8_out),
    .in8(bit_extender_9_out), .in9(bit_extender_10_out), .in10(bit_extender_11_out), .in11({A, B}),
    .in12(bit_extender_12_out), .in13(bit_extender_13_out), .in14(bit_extender_14_out),
    .in15(bit_extender_15_out), .out(ALUoutput), .sel(SELECT_01));  // open: en
  Hex_Digit_Display hex_digit_display_7 (.value(SELECT_01));  // open: dp
  Hex_Digit_Display hex_digit_display_8 (.value(ALUoutput[3:0]));  // open: dp
  Hex_Digit_Display hex_digit_display_9 (.value(ALUoutput[7:4]));  // open: dp
  Demultiplexer #(.select(4), .width(16)) demultiplexer_1 (
    .out0(demultiplexer_1_out0), .out1(Store), .out2(demultiplexer_1_out2), .out3(demultiplexer_1_out3),
    .out4(demultiplexer_1_out4), .out5(demultiplexer_1_out5), .out6(demultiplexer_1_out6),
    .out7(demultiplexer_1_out7), .out8(demultiplexer_1_out8), .out9(demultiplexer_1_out9),
    .out10(demultiplexer_1_out10), .out11(Exchange), .out12(demultiplexer_1_out12),
    .out13(demultiplexer_1_out13), .out14(demultiplexer_1_out14), .out15(demultiplexer_1_out15),
    .in(ALUoutput), .sel(SELECT_01));  // open: en
  xor odd_parity_1 (OddPriority, ALUoutput[15], ALUoutput[14], ALUoutput[13], ALUoutput[12], ALUoutput[11], ALUoutput[10], ALUoutput[9], ALUoutput[8], ALUoutput[7], ALUoutput[6], ALUoutput[5], ALUoutput[4], ALUoutput[3], ALUoutput[2], ALUoutput[1], ALUoutput[0]);
  assign Register = demultiplexer_1_out0 | demultiplexer_1_out2 | demultiplexer_1_out3 | demultiplexer_1_out4 | demultiplexer_1_out5 | demultiplexer_1_out6 | demultiplexer_1_out7 | demultiplexer_1_out8 | demultiplexer_1_out9 | demultiplexer_1_out10 | demultiplexer_1_out12 | demultiplexer_1_out13 | demultiplexer_1_out14 | demultiplexer_1_out15;  // OR_Gate or_5, 16 bits wide
  xnor even_parity_1 (evenParity, ALUoutput[15], ALUoutput[14], ALUoutput[13], ALUoutput[12], ALUoutput[11], ALUoutput[10], ALUoutput[9], ALUoutput[8], ALUoutput[7], ALUoutput[6], ALUoutput[5], ALUoutput[4], ALUoutput[3], ALUoutput[2], ALUoutput[1], ALUoutput[0]);
  Hex_Digit_Display hex_digit_display_10 (.value(Register[15:12]));  // open: dp
  Hex_Digit_Display hex_digit_display_11 (.value(Register[7:4]));  // open: dp
  Hex_Digit_Display hex_digit_display_12 (.value(Register[11:8]));  // open: dp
  Hex_Digit_Display hex_digit_display_13 (.value(Exchange[11:8]));  // open: dp
  Hex_Digit_Display hex_digit_display_14 (.value(Exchange[15:12]));  // open: dp
  Hex_Digit_Display hex_digit_display_15 (.value(Store[15:12]));  // open: dp
  Hex_Digit_Display hex_digit_display_16 (.value(Store[11:8]));  // open: dp
  Hex_Digit_Display hex_digit_display_17 (.value(Register[3:0]));  // open: dp
  Hex_Digit_Display hex_digit_display_18 (.value(Exchange[7:4]));  // open: dp
  Hex_Digit_Display hex_digit_display_19 (.value(Exchange[3:0]));  // open: dp
  Hex_Digit_Display hex_digit_display_20 (.value(Store[3:0]));  // open: dp
  Hex_Digit_Display hex_digit_display_21 (.value(Store[7:4]));  // open: dp

  assign Negative = ALUoutput[15];

  // Notes on the sheet:
  //   Exchange
  //   BitExtender
  //   Increment-----------------------------
  //   Decrement-----------------------
  //   Load
  //   Store
  //   Add
  //   Sub
  //   Mul
  //   Div
  //   And
  //   OR
  //   Not
  //   ShiftRight
  //   ShiftLeft
  //   Rotateright
  //   RotateLeft
  //   ALU-8bit 
  //   0-adder|1-sub|2-mpy|3-div|4-and|5-or|6-xnor|7-xor|8-lls|9-lrs|10-ars|11-rr|12-rl
endmodule

module Register (
  input  [7:0] Data_in,
  input  R_W,
  input  [3:0] input01,
  input  [3:0] Input_02,
  input  Clock,
  output [7:0] Regi_out_01,
  output [7:0] Regi_out_02
);

  wire decoder_1_out0, decoder_1_out1, decoder_1_out2, decoder_1_out3, decoder_1_out4, decoder_1_out5,
       decoder_1_out6, decoder_1_out7, decoder_1_out8, decoder_1_out9, decoder_1_out10, decoder_1_out11,
       decoder_1_out12, decoder_1_out13, decoder_1_out14, decoder_1_out15, not_1_out;
  wire [7:0] R0_q, R1_q, R2_q, R3_q, R4_q, R5_q, R6_q, R7_q, R8_q, R9_q, R10_q, R11_q, R12_q, R13_q, R14_q,
       R15_q;

  Hex_Digit_Display hex_digit_display_1 (.value(Data_in[7:4]));  // open: dp
  Hex_Digit_Display hex_digit_display_2 (.value(Data_in[3:0]));  // open: dp
  Hex_Digit_Display hex_digit_display_3 (.value(Input_02));  // open: dp
  Decoder #(.select(4), .disabled(0)) decoder_1 (
    .out0(decoder_1_out0), .out1(decoder_1_out1), .out2(decoder_1_out2), .out3(decoder_1_out3),
    .out4(decoder_1_out4), .out5(decoder_1_out5), .out6(decoder_1_out6), .out7(decoder_1_out7),
    .out8(decoder_1_out8), .out9(decoder_1_out9), .out10(decoder_1_out10), .out11(decoder_1_out11),
    .out12(decoder_1_out12), .out13(decoder_1_out13), .out14(decoder_1_out14), .out15(decoder_1_out15),
    .sel(input01), .en(not_1_out));
  not not_1 (not_1_out, R_W);
  Hex_Digit_Display hex_digit_display_4 (.value(input01));  // open: dp
  Register_part R0 (.D(Data_in), .en(decoder_1_out0), .Q(R0_q), .clk(Clock));  // open: clr
  Register_part R2 (.D(Data_in), .en(decoder_1_out2), .Q(R2_q), .clk(Clock));  // open: clr
  Register_part R4 (.D(Data_in), .en(decoder_1_out4), .Q(R4_q), .clk(Clock));  // open: clr
  Register_part R6 (.D(Data_in), .en(decoder_1_out6), .Q(R6_q), .clk(Clock));  // open: clr
  Register_part R8 (.D(Data_in), .en(decoder_1_out8), .Q(R8_q), .clk(Clock));  // open: clr
  Register_part R10 (.D(Data_in), .en(decoder_1_out10), .Q(R10_q), .clk(Clock));  // open: clr
  Register_part R12 (.D(Data_in), .en(decoder_1_out12), .Q(R12_q), .clk(Clock));  // open: clr
  Register_part R14 (.D(Data_in), .en(decoder_1_out14), .Q(R14_q), .clk(Clock));  // open: clr
  Register_part R1 (.D(Data_in), .en(decoder_1_out1), .Q(R1_q), .clk(Clock));  // open: clr
  Register_part R3 (.D(Data_in), .en(decoder_1_out3), .Q(R3_q), .clk(Clock));  // open: clr
  Register_part R5 (.D(Data_in), .en(decoder_1_out5), .Q(R5_q), .clk(Clock));  // open: clr
  Register_part R7 (.D(Data_in), .en(decoder_1_out7), .Q(R7_q), .clk(Clock));  // open: clr
  Register_part R9 (.D(Data_in), .en(decoder_1_out9), .Q(R9_q), .clk(Clock));  // open: clr
  Register_part R11 (.D(Data_in), .en(decoder_1_out11), .Q(R11_q), .clk(Clock));  // open: clr
  Register_part R13 (.D(Data_in), .en(decoder_1_out13), .Q(R13_q), .clk(Clock));  // open: clr
  Register_part R15 (.D(Data_in), .en(decoder_1_out15), .Q(R15_q), .clk(Clock));  // open: clr
  Multiplexer #(.select(4), .width(8), .disabled(0)) multiplexer_1 (
    .in0(R0_q), .in1(R1_q), .in2(R2_q), .in3(R3_q), .in4(R4_q), .in5(R5_q), .in6(R6_q), .in7(R7_q),
    .in8(R8_q), .in9(R9_q), .in10(R10_q), .in11(R11_q), .in12(R12_q), .in13(R13_q), .in14(R14_q),
    .in15(R15_q), .out(Regi_out_01), .sel(input01), .en(R_W));
  Hex_Digit_Display hex_digit_display_5 (.value(Regi_out_01[7:4]));  // open: dp
  Hex_Digit_Display hex_digit_display_6 (.value(Regi_out_02[7:4]));  // open: dp
  Multiplexer #(.select(4), .width(8), .disabled(0)) multiplexer_2 (
    .in0(R0_q), .in1(R1_q), .in2(R2_q), .in3(R3_q), .in4(R4_q), .in5(R5_q), .in6(R6_q), .in7(R7_q),
    .in8(R8_q), .in9(R9_q), .in10(R10_q), .in11(R11_q), .in12(R12_q), .in13(R13_q), .in14(R14_q),
    .in15(R15_q), .out(Regi_out_02), .sel(Input_02), .en(R_W));
  Hex_Digit_Display hex_digit_display_7 (.value(Regi_out_01[3:0]));  // open: dp
  Hex_Digit_Display hex_digit_display_8 (.value(Regi_out_02[3:0]));  // open: dp

  // Notes on the sheet:
  //   Register (4bits)
  //   Regi_Out_01
  //   Regi_out_02
endmodule

module selector (
  input  [15:0] Input,
  output Output
);

  wire bit_extender_1_out, or_1_out;

  or or_1 (or_1_out, Input[0], Input[1], Input[2], Input[3], Input[4], Input[5], Input[6], Input[7], Input[8], Input[9], Input[10], Input[11], Input[12], Input[13], Input[14], Input[15]);
  Comparator #(.width(1), .mode("unsigned")) comparator_1 (
    .a(or_1_out), .b(bit_extender_1_out), .eq(Output));  // open: gt, lt
  Bit_Extender #(.in_width(1), .out_width(1)) bit_extender_1 (.in(1'b1), .out(bit_extender_1_out));
endmodule

module Program_counter (
  input  [11:0] PC_INput,
  input  PC_enable,
  input  Clock,
  input  PC_reset,
  output [11:0] PC_OUT
);

  wire [11:0] adder_1_out;

  Hex_Digit_Display hex_digit_display_1 (.value(PC_INput[11:8]));  // open: dp
  Hex_Digit_Display hex_digit_display_2 (.value(PC_INput[3:0]));  // open: dp
  Hex_Digit_Display hex_digit_display_3 (.value(PC_INput[7:4]));  // open: dp
  Adder #(.width(12)) adder_1 (.a(PC_INput), .b(PC_OUT), .out(adder_1_out), .cin(1'b1));  // open: cout
  Hex_Digit_Display hex_digit_display_4 (.value(PC_OUT[7:4]));  // open: dp
  Hex_Digit_Display hex_digit_display_5 (.value(PC_OUT[11:8]));  // open: dp
  Register_part #(.width(12)) register_1 (.D(adder_1_out), .en(PC_enable), .Q(PC_OUT), .clk(Clock), .clr(PC_reset));
  Hex_Digit_Display hex_digit_display_6 (.value(PC_OUT[3:0]));  // open: dp
endmodule

module cycle (
  input  PC_enable,
  input  Clock,
  input  PC_reset,
  output [2:0] PC_OUT
);

  wire [2:0] adder_1_out;
  wire [3:0] undriven, undriven_2;

  Adder #(.width(3)) adder_1 (.a(3'b000), .b(PC_OUT), .out(adder_1_out), .cin(1'b1));  // open: cout
  Hex_Digit_Display hex_digit_display_1 (.value(undriven));  // open: dp
  Register_part #(.width(3)) register_1 (.D(adder_1_out), .en(PC_enable), .Q(PC_OUT), .clk(Clock), .clr(PC_reset));
  Hex_Digit_Display hex_digit_display_2 (.value(undriven_2));  // open: dp
endmodule
