// Logisim project 1 Bit ram cell.circ as structural Verilog: 2 circuits, main circuit main
module main (
  input  R_W_prime,
  input  Data,
  input  Select,
  input  in_4,
  output Output
);

  wire and_1_out, and_2_out, not_1_out, not_2_out, s_r_ff_1_q;

  not not_1 (not_1_out, R_W_prime);
  not not_2 (not_2_out, Data);
  and and_1 (and_1_out, Data, not_1_out);
  and and_2 (and_2_out, not_2_out, not_1_out);
  S_R_Flip_Flop s_r_ff_1 (
    .S(and_1_out), .clk(in_4), .R(and_2_out), .Q(s_r_ff_1_q), .en(Select));  // open: Qn, preset, reset
  and and_3 (Output, s_r_ff_1_q, R_W_prime);
endmodule

module jai_shree_ram (
  input  R_W_prime,
  input  Data,
  input  Select,
  output out_4,
  output out_5,
  output out_6,
  output out_7
);

  wire clock_1_out, decoder_1_out0, decoder_1_out1;

  Clock clock_1 (.out(clock_1_out));
  Decoder #(.enable("false")) decoder_1 (.out0(decoder_1_out0), .out1(decoder_1_out1), .sel(Select));
  main main_1 (.in_4(clock_1_out), .R_W_prime(R_W_prime), .Data(Data), .Select(decoder_1_out0), .Output(out_4));
  main main_2 (.in_4(clock_1_out), .R_W_prime(R_W_prime), .Data(Data), .Select(decoder_1_out1), .Output(out_7));
  main main_3 (.in_4(clock_1_out), .R_W_prime(R_W_prime), .Data(Data), .Select(decoder_1_out0), .Output(out_5));
  main main_4 (.in_4(clock_1_out), .R_W_prime(R_W_prime), .Data(Data), .Select(decoder_1_out1), .Output(out_6));
endmodule
