// Logisim project 1bit_ram_cell.circ as structural Verilog
module main (
  input  [1:0] data,
  input  r_w_prime,
  input  select,
  output out_4,
  output out_5
);

  wire clock_1_out, decoder_1_out0, decoder_1_out1, test_1_out_5, test_2_out_5, test_3_out_5, test_4_out_5;

  Decoder #(.enable("false")) decoder_1 (.out0(decoder_1_out0), .out1(decoder_1_out1), .sel(select));
  Clock clock_1 (.out(clock_1_out));
  test test_1 (
    .in_4(clock_1_out), .R_W_prime(r_w_prime), .Data(data[1]), .Select(decoder_1_out0), .out_5(test_1_out_5));
  test test_2 (
    .in_4(clock_1_out), .R_W_prime(r_w_prime), .Data(data[1]), .Select(decoder_1_out1), .out_5(test_2_out_5));
  test test_3 (
    .in_4(clock_1_out), .R_W_prime(r_w_prime), .Data(data[0]), .Select(decoder_1_out0), .out_5(test_3_out_5));
  test test_4 (
    .in_4(clock_1_out), .R_W_prime(r_w_prime), .Data(data[0]), .Select(decoder_1_out1), .out_5(test_4_out_5));
  Multiplexer #(.enable("false")) multiplexer_1 (.in0(test_1_out_5), .in1(test_2_out_5), .out(out_4), .sel(select));
  Multiplexer #(.enable("false")) multiplexer_2 (.in0(test_3_out_5), .in1(test_4_out_5), .out(out_5), .sel(select));
endmodule

module _2_2_ram_cell (
  input  r_w_prime,
  input  data,
  input  data_2,
  input  select,
  output out_5,
  output out_6
);

  wire clock_1_out, decoder_1_out0, decoder_1_out1, test_1_out_5, test_2_out_5, test_3_out_5, test_4_out_5;

  Decoder #(.enable("false")) decoder_1 (.out0(decoder_1_out0), .out1(decoder_1_out1), .sel(select));
  Clock clock_1 (.out(clock_1_out));
  test test_1 (.in_4(clock_1_out), .R_W_prime(r_w_prime), .Data(data), .Select(decoder_1_out0), .out_5(test_1_out_5));
  test test_2 (.in_4(clock_1_out), .R_W_prime(r_w_prime), .Data(data), .Select(decoder_1_out1), .out_5(test_2_out_5));
  test test_3 (.in_4(clock_1_out), .R_W_prime(r_w_prime), .Data(data_2), .Select(decoder_1_out0), .out_5(test_3_out_5));
  test test_4 (.in_4(clock_1_out), .R_W_prime(r_w_prime), .Data(data_2), .Select(decoder_1_out1), .out_5(test_4_out_5));
  Multiplexer #(.enable("false")) multiplexer_1 (.in0(test_1_out_5), .in1(test_2_out_5), .out(out_5), .sel(select));
  Multiplexer #(.enable("false")) multiplexer_2 (.in0(test_3_out_5), .in1(test_4_out_5), .out(out_6), .sel(select));
endmodule

// 1 bit
module test (
  input  R_W_prime,
  input  Data,
  input  Select,
  input  in_4,
  output out_5
);

  wire A_out, B_out, not_1_out, not_2_out, s_r_ff_1_q;

  not not_1 (not_1_out, R_W_prime);
  not not_2 (not_2_out, Data);
  and A (A_out, Data, not_1_out);
  and B (B_out, not_2_out, not_1_out);
  S_R_Flip_Flop s_r_ff_1 (.S(A_out), .clk(in_4), .R(B_out), .Q(s_r_ff_1_q), .en(Select));  // open: Qn, preset, reset
  and OUTPUT (out_5, s_r_ff_1_q, R_W_prime);
endmodule
