// Logisim project Activity 1.circ as structural Verilog: 4 circuits, main circuit main
// MAR
module main (
  input  [7:0] in_1,
  input  PC_Reset,
  output [7:0] PC,
  output [15:0] out_4
);

  wire clock_1_out, not_1_out, PC_Shift_out, R_W_Shift_out;
  wire [7:0] MAR_q, RA_q, RB_q, Register_out_5, RZ_q;
  wire [15:0] IR_q, MBR_q, rom_1_data;
  wire [15:8] RZ_q_2;

  Clock clock_1 (.out(clock_1_out));
  Program_counter u_PC (.in_1(in_1), .PC_Enable(PC_Shift_out), .PC_reset(PC_Reset), .Clock(clock_1_out), .out_5(PC));
  Register MAR (.D(PC), .en(PC_Shift_out), .Q(MAR_q), .clk(clock_1_out), .clr(PC_Reset));
  Shift_Register #(.length(5)) PC_Shift (
    .in(PC_Shift_out), .clk(clock_1_out), .out(PC_Shift_out));  // open: shift, load, clr, d0, q0, d1, q1, d2, q2, d3, q3, d4, q4
  ROM #(.dataWidth(16)) rom_1 (.addr(MAR_q), .data(rom_1_data));  // open: sel
  Shift_Register #(.length(5)) R_W_Shift (
    .in(R_W_Shift_out), .clk(clock_1_out), .out(R_W_Shift_out));  // open: shift, load, clr, d0, q0, d1, q1, d2, q2, d3, q3, d4, q4
  Register #(.width(16)) MBR (.D(rom_1_data), .Q(MBR_q), .clk(clock_1_out), .clr(PC_Reset));  // open: en
  Register #(.width(16)) IR (.D(MBR_q), .Q(IR_q), .clk(clock_1_out), .clr(PC_Reset));  // open: en
  not not_1 (not_1_out, R_W_Shift_out);
  Register RA (.D(Register_out_5), .Q(RA_q), .clk(clock_1_out), .clr(PC_Reset));  // open: en
  Register RB (.D(RB_q), .Q(RB_q), .clk(clock_1_out), .clr(PC_Reset));  // open: en
  Register_file Register (
    .Input(RZ_q), .R_W(R_W_Shift_out), .RX(IR_q[10:8]), .Clock(clock_1_out), .out_5(Register_out_5));
  RAM #(.bus("separate")) ram_1 (
    .addr(IR_q[7:0]), .din(RB_q), .data(RB_q), .str(not_1_out), .clk(clock_1_out), .ld(R_W_Shift_out));  // open: sel, clr
  Register #(.width(16)) RZ (.D(out_4), .Q({RZ_q_2, RZ_q}), .clk(clock_1_out), .clr(PC_Reset));  // open: en
  ALU ALU (.A(RA_q), .B(RB_q), ._1(IR_q[14:11]), .out_4(out_4));
  Hex_Digit_Display hex_digit_display_1 (.value(out_4[15:12]));  // open: dp
  Hex_Digit_Display hex_digit_display_2 (.value(out_4[7:4]));  // open: dp
  Hex_Digit_Display hex_digit_display_3 (.value(out_4[11:8]));  // open: dp
  Hex_Digit_Display hex_digit_display_4 (.value(out_4[3:0]));  // open: dp

  // Notes on the sheet:
  //   Code Memory
  //   contents of rom_1 (hex, n*v repeats v):
  //   3804
  //   Data Memory
  //   Result
endmodule

module Register_file (
  input  [7:0] Input,
  input  R_W,
  input  [2:0] RX,
  input  Clock,
  output [7:0] out_5
);

  wire decoder_1_out0, decoder_1_out1, decoder_1_out2, decoder_1_out3, decoder_1_out4, decoder_1_out5,
       decoder_1_out6, decoder_1_out7, not_1_out;
  wire [7:0] R0_q, R1_q, R2_q, R3_q, R4_q, R5_q, R6_q, R7_q;

  Hex_Digit_Display hex_digit_display_1 (.value(Input[3:0]));  // open: dp
  Hex_Digit_Display hex_digit_display_2 (.value(Input[7:4]));  // open: dp
  Decoder #(.select(3), .disabled(0)) decoder_1 (
    .out0(decoder_1_out0), .out1(decoder_1_out1), .out2(decoder_1_out2), .out3(decoder_1_out3),
    .out4(decoder_1_out4), .out5(decoder_1_out5), .out6(decoder_1_out6), .out7(decoder_1_out7), .sel(RX),
    .en(not_1_out));
  not not_1 (not_1_out, R_W);
  Register R0 (.D(Input), .en(decoder_1_out0), .Q(R0_q), .clk(Clock));  // open: clr
  Register R1 (.D(Input), .en(decoder_1_out1), .Q(R1_q), .clk(Clock));  // open: clr
  Register R2 (.D(Input), .en(decoder_1_out2), .Q(R2_q), .clk(Clock));  // open: clr
  Register R3 (.D(Input), .en(decoder_1_out3), .Q(R3_q), .clk(Clock));  // open: clr
  Register R4 (.D(Input), .en(decoder_1_out4), .Q(R4_q), .clk(Clock));  // open: clr
  Register R5 (.D(Input), .en(decoder_1_out5), .Q(R5_q), .clk(Clock));  // open: clr
  Register R6 (.D(Input), .en(decoder_1_out6), .Q(R6_q), .clk(Clock));  // open: clr
  Register R7 (.D(Input), .en(decoder_1_out7), .Q(R7_q), .clk(Clock));  // open: clr
  Multiplexer #(.select(3), .width(8)) multiplexer_1 (
    .in0(R0_q), .in1(R1_q), .in2(R2_q), .in3(R3_q), .in4(R4_q), .in5(R5_q), .in6(R6_q), .in7(R7_q),
    .out(out_5), .sel(RX), .en(R_W));

  // Notes on the sheet:
  //   fLOATING STATE DECODER-OFF IT IS NOT HIGH OR LOW STATE
endmodule

module Program_counter (
  input  [7:0] in_1,
  input  PC_Enable,
  input  PC_reset,
  input  Clock,
  output [7:0] out_5
);

  wire [7:0] adder_1_out;

  Adder adder_1 (.a(in_1), .b(out_5), .out(adder_1_out), .cin(1'b1));  // open: cout
  Register register_1 (.D(adder_1_out), .en(PC_Enable), .Q(out_5), .clk(Clock), .clr(PC_reset));
  Hex_Digit_Display hex_digit_display_1 (.value(out_5[7:4]));  // open: dp
  Hex_Digit_Display hex_digit_display_2 (.value(out_5[3:0]));  // open: dp

  // Notes on the sheet:
  //   Program Counter
endmodule

module ALU (
  input  [7:0] A,
  input  [7:0] B,
  input  [3:0] _1,
  output [15:0] out_4
);

  wire adder_1_cout, subtractor_1_bout;
  wire [2:0] bit_extender_1_out;
  wire [7:0] adder_1_out, and_1_out, bit_extender_2_out, bit_extender_3_out, divider_1_out, divider_1_rem,
       multiplier_1_cout, multiplier_1_out, nor_1_out, or_1_out, shifter_1_out, shifter_2_out, shifter_3_out,
       shifter_4_out, shifter_5_out, subtractor_1_out, xnor_1_out;
  wire [15:0] bit_extender_4_out, bit_extender_5_out, bit_extender_6_out, bit_extender_7_out,
       bit_extender_8_out, bit_extender_9_out, bit_extender_10_out, bit_extender_11_out, bit_extender_12_out,
       undriven, undriven_2, undriven_3;

  Hex_Digit_Display hex_digit_display_1 (.value(A[7:4]));  // open: dp
  Hex_Digit_Display hex_digit_display_2 (.value(B[7:4]));  // open: dp
  Hex_Digit_Display hex_digit_display_3 (.value(A[3:0]));  // open: dp
  Hex_Digit_Display hex_digit_display_4 (.value(B[3:0]));  // open: dp
  Bit_Extender #(.out_width(3)) bit_extender_1 (.in(B), .out(bit_extender_1_out));
  Adder adder_1 (.a(A), .b(B), .out(adder_1_out), .cout(adder_1_cout));  // open: cin
  Subtractor subtractor_1 (.a(A), .b(B), .out(subtractor_1_out), .bout(subtractor_1_bout));  // open: bin
  Multiplier multiplier_1 (.a(A), .b(B), .out(multiplier_1_out), .cout(multiplier_1_cout));  // open: cin
  Divider divider_1 (.a(A), .b(B), .out(divider_1_out), .rem(divider_1_rem));  // open: upper
  assign and_1_out = A & B;  // AND_Gate and_1, 8 bits wide
  assign or_1_out = A | B;  // OR_Gate or_1, 8 bits wide
  assign xnor_1_out = ~(A ^ B);  // XNOR_Gate xnor_1, 8 bits wide
  assign nor_1_out = ~(A | B);  // NOR_Gate nor_1, 8 bits wide
  Shifter shifter_1 (.in(A), .\dist (bit_extender_1_out), .out(shifter_1_out));
  Shifter #(.shift("lr")) shifter_2 (.in(A), .\dist (bit_extender_1_out), .out(shifter_2_out));
  Shifter #(.shift("ar")) shifter_3 (.in(A), .\dist (bit_extender_1_out), .out(shifter_3_out));
  Shifter #(.shift("rl")) shifter_4 (.in(A), .\dist (bit_extender_1_out), .out(shifter_4_out));
  Shifter #(.shift("rr")) shifter_5 (.in(A), .\dist (bit_extender_1_out), .out(shifter_5_out));
  assign bit_extender_2_out = {{7{1'b0}}, adder_1_cout};  // Bit_Extender bit_extender_2
  assign bit_extender_3_out = {{7{1'b0}}, subtractor_1_bout};  // Bit_Extender bit_extender_3
  assign bit_extender_4_out = {{8{1'b0}}, and_1_out};  // Bit_Extender bit_extender_4
  assign bit_extender_5_out = {{8{1'b0}}, or_1_out};  // Bit_Extender bit_extender_5
  assign bit_extender_6_out = {{8{1'b0}}, xnor_1_out};  // Bit_Extender bit_extender_6
  assign bit_extender_7_out = {{8{1'b0}}, nor_1_out};  // Bit_Extender bit_extender_7
  assign bit_extender_8_out = {{8{1'b0}}, shifter_1_out};  // Bit_Extender bit_extender_8
  assign bit_extender_9_out = {{8{1'b0}}, shifter_2_out};  // Bit_Extender bit_extender_9
  assign bit_extender_10_out = {{8{1'b0}}, shifter_3_out};  // Bit_Extender bit_extender_10
  assign bit_extender_11_out = {{8{1'b0}}, shifter_4_out};  // Bit_Extender bit_extender_11
  assign bit_extender_12_out = {{8{1'b0}}, shifter_5_out};  // Bit_Extender bit_extender_12
  Multiplexer #(.select(4), .width(16), .enable("false")) multiplexer_1 (
    .in0({bit_extender_2_out, adder_1_out}), .in1({bit_extender_3_out, subtractor_1_out}),
    .in2({multiplier_1_cout, multiplier_1_out}), .in3({divider_1_rem, divider_1_out}),
    .in4(bit_extender_4_out), .in5(bit_extender_5_out), .in6(bit_extender_6_out), .in7(bit_extender_7_out),
    .in8(bit_extender_8_out), .in9(bit_extender_9_out), .in10(bit_extender_10_out),
    .in11(bit_extender_11_out), .in12(bit_extender_12_out), .in13(undriven), .in14(undriven_2),
    .in15(undriven_3), .out(out_4), .sel(_1));
  Hex_Digit_Display hex_digit_display_5 (.value(out_4[15:12]));  // open: dp
  Hex_Digit_Display hex_digit_display_6 (.value(out_4[11:8]));  // open: dp
  Hex_Digit_Display hex_digit_display_7 (.value(_1));  // open: dp
  Hex_Digit_Display hex_digit_display_8 (.value(out_4[7:4]));  // open: dp
  Hex_Digit_Display hex_digit_display_9 (.value(out_4[3:0]));  // open: dp

  // Notes on the sheet:
  //   BitExtender
  //   ALU-8bit 
  //   Add
  //   Sub
  //   Mul
  //   Div
  //   And
  //   OR
  //   XNor
  //   NOR
  //   LogicLeft
  //   LogicRight
  //   ArithRight
  //   RotateLeft
  //   Rotateright
  //   0-adder|1-sub|2-mpy|3-div|4-and|5-or|6-xnor|7-xor|8-lls|9-lrs|10-ars|11-rr|12-rl
endmodule
