// Logisim project Mux.circ as structural Verilog: 2 circuits, main circuit main
module main (
  input  [3:0] A,
  input  [3:0] B,
  input  [2:0] Opcode,
  input  [10:0] in_4,
  output [7:0] Output,
  output [7:0] Output_2
);

  Hex_Digit_Display hex_digit_display_1 (.value(A));  // open: dp
  Hex_Digit_Display hex_digit_display_2 (.value(B));  // open: dp
  Hex_Digit_Display hex_digit_display_3 (.value(Output[7:4]));  // open: dp
  ALU ALU (.A_4_bits(A), .B_4_bits(B), .OPcode_2_bits(Opcode), .Output_8_bits(Output));
  Hex_Digit_Display hex_digit_display_4 (.value(Output[3:0]));  // open: dp
  ALU ALU_2 (.A_4_bits(in_4[3:0]), .B_4_bits(in_4[7:4]), .OPcode_2_bits(in_4[10:8]), .Output_8_bits(Output_2));
endmodule

module ALU (
  input  [3:0] A_4_bits,
  input  [3:0] B_4_bits,
  input  [2:0] OPcode_2_bits,
  output [7:0] Output_8_bits
);

  wire adder_1_cout, subtractor_1_bout;
  wire [3:0] adder_1_out, and_1_out, bit_extender_1_out, bit_extender_2_out, divider_1_out, divider_1_rem,
       multiplier_1_cout, multiplier_1_out, nor_1_out, or_1_out, subtractor_1_out, xor_1_out;

  Hex_Digit_Display hex_digit_display_1 (.value(A_4_bits));  // open: dp
  Hex_Digit_Display hex_digit_display_2 (.value(B_4_bits));  // open: dp
  Adder #(.width(4)) adder_1 (.a(A_4_bits), .b(B_4_bits), .out(adder_1_out), .cout(adder_1_cout));  // open: cin
  Subtractor #(.width(4)) subtractor_1 (
    .a(A_4_bits), .b(B_4_bits), .out(subtractor_1_out), .bout(subtractor_1_bout));  // open: bin
  Multiplier #(.width(4)) multiplier_1 (
    .a(A_4_bits), .b(B_4_bits), .out(multiplier_1_out), .cout(multiplier_1_cout));  // open: cin
  Divider #(.width(4)) divider_1 (.a(A_4_bits), .b(B_4_bits), .out(divider_1_out), .rem(divider_1_rem));  // open: upper
  assign or_1_out = A_4_bits | B_4_bits;  // OR_Gate or_1, 4 bits wide
  assign and_1_out = A_4_bits & B_4_bits;  // AND_Gate and_1, 4 bits wide
  assign nor_1_out = ~(A_4_bits | B_4_bits);  // NOR_Gate nor_1, 4 bits wide
  assign xor_1_out = A_4_bits ^ B_4_bits;  // XOR_Gate xor_1, 4 bits wide
  assign bit_extender_1_out = {{3{1'b0}}, adder_1_cout};  // Bit_Extender bit_extender_1
  assign bit_extender_2_out = {{3{1'b0}}, subtractor_1_bout};  // Bit_Extender bit_extender_2
  Multiplexer #(.select(3), .width(8), .enable("false")) multiplexer_1 (
    .in0({bit_extender_1_out, adder_1_out}), .in1({bit_extender_2_out, subtractor_1_out}),
    .in2({multiplier_1_cout, multiplier_1_out}), .in3({divider_1_rem, divider_1_out}),
    .in4({4'b0000, or_1_out}), .in5({4'b0000, and_1_out}), .in6({4'b0000, nor_1_out}),
    .in7({4'b0000, xor_1_out}), .out(Output_8_bits), .sel(OPcode_2_bits));
  Hex_Digit_Display hex_digit_display_3 (.value(Output_8_bits[3:0]));  // open: dp
  Hex_Digit_Display hex_digit_display_4 (.value(Output_8_bits[7:4]));  // open: dp

  // Notes on the sheet:
  //   Subtractor--------------------------->
  //   Multiplier--------------------------->
  //   Divider--------------------------->
  //   Bit extender--------------------------->
  //   Adder
  //   Multiplexer
endmodule
