// Logisim project Processor.circ as structural Verilog: 5 circuits, main circuit main
module main (
  input  [7:0] Datain_0_7,
  input  in_2,
  input  R_W,
  input  [7:0] in_4,
  input  [7:0] Datain_8bit,
  output [15:0] out_6
);

  wire Clock_out, not_1_out, shift_register_1_out;
  wire [3:0] ram_1_data, ram_1_data_2, register_file_1_out_5, register_file_1_out_5_2;
  wire [7:0] program_counter_1_out_5;
  wire [14:0] rom_1_data;

  Shift_Register #(.length(4)) shift_register_1 (
    .in(shift_register_1_out), .clk(Clock_out), .out(shift_register_1_out));  // open: shift, load, clr, d0, q0, d1, q1, d2, q2, d3, q3
  Program_Counter program_counter_1 (
    .in_1(in_4), .PC_reset(in_2), .Clock(shift_register_1_out), .PC_Enable(Clock_out),
    .out_5(program_counter_1_out_5));
  Clock Clock (.out(Clock_out));
  ROM #(.dataWidth(15)) rom_1 (.addr(program_counter_1_out_5), .data(rom_1_data));  // open: sel
  not not_1 (not_1_out, R_W);
  Hex_Digit_Display hex_digit_display_1 (.value(register_file_1_out_5_2));  // open: dp
  Hex_Digit_Display hex_digit_display_2 (.value(register_file_1_out_5));  // open: dp
  Hex_Digit_Display hex_digit_display_3 (.value(ram_1_data_2));  // open: dp
  Register_file register_file_1 (
    .Input(Datain_0_7), .R_W(R_W), .RX(rom_1_data[10:8]), .Clock(Clock_out),
    .out_5({register_file_1_out_5_2, register_file_1_out_5}));
  RAM #(.bus("separate")) ram_1 (
    .addr(rom_1_data[7:0]), .din(Datain_8bit), .data({ram_1_data_2, ram_1_data}), .str(not_1_out),
    .clk(Clock_out), .ld(R_W));  // open: sel, clr
  Hex_Digit_Display hex_digit_display_4 (.value(ram_1_data));  // open: dp
  Hex_Digit_Display hex_digit_display_5 (.value(out_6[11:8]));  // open: dp
  Hex_Digit_Display hex_digit_display_6 (.value(out_6[15:12]));  // open: dp
  ALU alu_1 (
    .A({register_file_1_out_5_2, register_file_1_out_5}), .B({ram_1_data_2, ram_1_data}),
    ._1(rom_1_data[14:11]), .out_4(out_6));
  Hex_Digit_Display hex_digit_display_7 (.value(out_6[7:4]));  // open: dp
  Hex_Digit_Display hex_digit_display_8 (.value(out_6[3:0]));  // open: dp

  // Notes on the sheet:
  //   contents of rom_1 (hex, n*v repeats v):
  //   3804 200 4301
  //   Processor
  //   Data Memory (RAM)
  //   Register
  //   ALU
endmodule

module ALU (
  input  [7:0] A,
  input  [7:0] B,
  input  [3:0] _1,
  output [15:0] out_4
);

  wire adder_1_cout, subtractor_1_bout;
  wire [2:0] bit_extender_1_out;
  wire [7:0] adder_1_out, and_1_out, bit_extender_2_out, bit_extender_3_out, divider_1_out, divider_1_rem,
       multiplier_1_cout, multiplier_1_out, nor_1_out, or_1_out, shifter_1_out, shifter_2_out, shifter_3_out,
       shifter_4_out, shifter_5_out, subtractor_1_out, xnor_1_out;
  wire [15:0] bit_extender_4_out, bit_extender_5_out, bit_extender_6_out, bit_extender_7_out,
       bit_extender_8_out, bit_extender_9_out, bit_extender_10_out, bit_extender_11_out, bit_extender_12_out,
       undriven, undriven_2, undriven_3;

  Hex_Digit_Display hex_digit_display_1 (.value(A[7:4]));  // open: dp
  Hex_Digit_Display hex_digit_display_2 (.value(B[7:4]));  // open: dp
  Hex_Digit_Display hex_digit_display_3 (.value(A[3:0]));  // open: dp
  Hex_Digit_Display hex_digit_display_4 (.value(B[3:0]));  // open: dp
  Bit_Extender #(.out_width(3)) bit_extender_1 (.in(B), .out(bit_extender_1_out));
  Adder adder_1 (.a(A), .b(B), .out(adder_1_out), .cout(adder_1_cout));  // open: cin
  Subtractor subtractor_1 (.a(A), .b(B), .out(subtractor_1_out), .bout(subtractor_1_bout));  // open: bin
  Multiplier multiplier_1 (.a(A), .b(B), .out(multiplier_1_out), .cout(multiplier_1_cout));  // open: cin
  Divider divider_1 (.a(A), .b(B), .out(divider_1_out), .rem(divider_1_rem));  // open: upper
  assign and_1_out = A & B;  // AND_Gate and_1, 8 bits wide
  assign or_1_out = A | B;  // OR_Gate or_1, 8 bits wide
  assign xnor_1_out = ~(A ^ B);  // XNOR_Gate xnor_1, 8 bits wide
  assign nor_1_out = ~(A | B);  // NOR_Gate nor_1, 8 bits wide
  Shifter shifter_1 (.in(A), .\dist (bit_extender_1_out), .out(shifter_1_out));
  Shifter #(.shift("lr")) shifter_2 (.in(A), .\dist (bit_extender_1_out), .out(shifter_2_out));
  Shifter #(.shift("ar")) shifter_3 (.in(A), .\dist (bit_extender_1_out), .out(shifter_3_out));
  Shifter #(.shift("rl")) shifter_4 (.in(A), .\dist (bit_extender_1_out), .out(shifter_4_out));
  Shifter #(.shift("rr")) shifter_5 (.in(A), .\dist (bit_extender_1_out), .out(shifter_5_out));
  assign bit_extender_2_out = {{7{1'b0}}, adder_1_cout};  // Bit_Extender bit_extender_2
  assign bit_extender_3_out = {{7{1'b0}}, subtractor_1_bout};  // Bit_Extender bit_extender_3
  assign bit_extender_4_out = {{8{1'b0}}, and_1_out};  // Bit_Extender bit_extender_4
  assign bit_extender_5_out = {{8{1'b0}}, or_1_out};  // Bit_Extender bit_extender_5
  assign bit_extender_6_out = {{8{1'b0}}, xnor_1_out};  // Bit_Extender bit_extender_6
  assign bit_extender_7_out = {{8{1'b0}}, nor_1_out};  // Bit_Extender bit_extender_7
  assign bit_extender_8_out = {{8{1'b0}}, shifter_1_out};  // Bit_Extender bit_extender_8
  assign bit_extender_9_out = {{8{1'b0}}, shifter_2_out};  // Bit_Extender bit_extender_9
  assign bit_extender_10_out = {{8{1'b0}}, shifter_3_out};  // Bit_Extender bit_extender_10
  assign bit_extender_11_out = {{8{1'b0}}, shifter_4_out};  // Bit_Extender bit_extender_11
  assign bit_extender_12_out = {{8{1'b0}}, shifter_5_out};  // Bit_Extender bit_extender_12
  Multiplexer #(.select(4), .width(16), .enable("false")) multiplexer_1 (
    .in0({bit_extender_2_out, adder_1_out}), .in1({bit_extender_3_out, subtractor_1_out}),
    .in2({multiplier_1_cout, multiplier_1_out}), .in3({divider_1_rem, divider_1_out}),
    .in4(bit_extender_4_out), .in5(bit_extender_5_out), .in6(bit_extender_6_out), .in7(bit_extender_7_out),
    .in8(bit_extender_8_out), .in9(bit_extender_9_out), .in10(bit_extender_10_out),
    .in11(bit_extender_11_out), .in12(bit_extender_12_out), .in13(undriven), .in14(undriven_2),
    .in15(undriven_3), .out(out_4), .sel(_1));
  Hex_Digit_Display hex_digit_display_5 (.value(out_4[11:8]));  // open: dp
  Hex_Digit_Display hex_digit_display_6 (.value(out_4[15:12]));  // open: dp
  Hex_Digit_Display hex_digit_display_7 (.value(_1));  // open: dp
  Hex_Digit_Display hex_digit_display_8 (.value(out_4[7:4]));  // open: dp
  Hex_Digit_Display hex_digit_display_9 (.value(out_4[3:0]));  // open: dp

  // Notes on the sheet:
  //   BitExtender
  //   ALU-8bit 
  //   Add
  //   Sub
  //   Mul
  //   Div
  //   And
  //   OR
  //   XNor
  //   NOR
  //   LogicLeft
  //   LogicRight
  //   ArithRight
  //   RotateLeft
  //   Rotateright
  //   0-adder|1-sub|2-mpy|3-div|4-and|5-or|6-xnor|7-xor|8-lls|9-lrs|10-ars|11-rr|12-rl
endmodule

module Register_file (
  input  [7:0] Input,
  input  R_W,
  input  [2:0] RX,
  input  Clock,
  output [7:0] out_5
);

  wire decoder_1_out0, decoder_1_out1, decoder_1_out2, decoder_1_out3, decoder_1_out4, decoder_1_out5,
       decoder_1_out6, decoder_1_out7, not_1_out;
  wire [7:0] R0_q, R1_q, R2_q, R3_q, R4_q, R5_q, R6_q, R7_q;

  Hex_Digit_Display hex_digit_display_1 (.value(Input[3:0]));  // open: dp
  Hex_Digit_Display hex_digit_display_2 (.value(Input[7:4]));  // open: dp
  Decoder #(.select(3), .disabled(0)) decoder_1 (
    .out0(decoder_1_out0), .out1(decoder_1_out1), .out2(decoder_1_out2), .out3(decoder_1_out3),
    .out4(decoder_1_out4), .out5(decoder_1_out5), .out6(decoder_1_out6), .out7(decoder_1_out7), .sel(RX),
    .en(not_1_out));
  not not_1 (not_1_out, R_W);
  Register R0 (.D(Input), .en(decoder_1_out0), .Q(R0_q), .clk(Clock));  // open: clr
  Register R1 (.D(Input), .en(decoder_1_out1), .Q(R1_q), .clk(Clock));  // open: clr
  Register R2 (.D(Input), .en(decoder_1_out2), .Q(R2_q), .clk(Clock));  // open: clr
  Register R3 (.D(Input), .en(decoder_1_out3), .Q(R3_q), .clk(Clock));  // open: clr
  Register R4 (.D(Input), .en(decoder_1_out4), .Q(R4_q), .clk(Clock));  // open: clr
  Register R5 (.D(Input), .en(decoder_1_out5), .Q(R5_q), .clk(Clock));  // open: clr
  Register R6 (.D(Input), .en(decoder_1_out6), .Q(R6_q), .clk(Clock));  // open: clr
  Register R7 (.D(Input), .en(decoder_1_out7), .Q(R7_q), .clk(Clock));  // open: clr
  Multiplexer #(.select(3), .width(8)) multiplexer_1 (
    .in0(R0_q), .in1(R1_q), .in2(R2_q), .in3(R3_q), .in4(R4_q), .in5(R5_q), .in6(R6_q), .in7(R7_q),
    .out(out_5), .sel(RX), .en(R_W));

  // Notes on the sheet:
  //   fLOATING STATE DECODER-OFF IT IS NOT HIGH OR LOW STATE
endmodule

module p (
  input  [7:0] Datain_0_7,
  input  [2:0] Rx,
  input  R_W,
  input  [3:0] OPCODE,
  input  [7:0] Address_0_8,
  input  [7:0] Datain_8bit,
  output [15:0] out_7
);

  wire Clock_out, not_1_out;
  wire [3:0] ram_1_data, ram_1_data_2, register_file_1_out_5, register_file_1_out_5_2;

  Clock Clock (.out(Clock_out));
  not not_1 (not_1_out, R_W);
  Hex_Digit_Display hex_digit_display_1 (.value(register_file_1_out_5));  // open: dp
  Hex_Digit_Display hex_digit_display_2 (.value(register_file_1_out_5_2));  // open: dp
  Hex_Digit_Display hex_digit_display_3 (.value(ram_1_data_2));  // open: dp
  Register_file register_file_1 (
    .Input(Datain_0_7), .R_W(R_W), .RX(Rx), .Clock(Clock_out),
    .out_5({register_file_1_out_5_2, register_file_1_out_5}));
  RAM #(.bus("separate")) ram_1 (
    .addr(Address_0_8), .din(Datain_8bit), .data({ram_1_data_2, ram_1_data}), .str(not_1_out),
    .clk(Clock_out), .ld(R_W));  // open: sel, clr
  Hex_Digit_Display hex_digit_display_4 (.value(ram_1_data));  // open: dp
  Hex_Digit_Display hex_digit_display_5 (.value(out_7[11:8]));  // open: dp
  Hex_Digit_Display hex_digit_display_6 (.value(out_7[15:12]));  // open: dp
  ALU alu_1 (
    .A({register_file_1_out_5_2, register_file_1_out_5}), .B({ram_1_data_2, ram_1_data}), ._1(OPCODE),
    .out_4(out_7));
  Hex_Digit_Display hex_digit_display_7 (.value(out_7[3:0]));  // open: dp
  Hex_Digit_Display hex_digit_display_8 (.value(out_7[7:4]));  // open: dp

  // Notes on the sheet:
  //   Register
  //   ALU
endmodule

module Program_Counter (
  input  [7:0] in_1,
  input  PC_Enable,
  input  PC_reset,
  input  Clock,
  output [7:0] out_5
);

  wire [7:0] adder_1_out;

  Adder adder_1 (.a(in_1), .b(out_5), .out(adder_1_out), .cin(1'b1));  // open: cout
  Register register_1 (.D(adder_1_out), .en(PC_Enable), .Q(out_5), .clk(Clock), .clr(PC_reset));
  Hex_Digit_Display hex_digit_display_1 (.value(out_5[3:0]));  // open: dp
  Hex_Digit_Display hex_digit_display_2 (.value(out_5[7:4]));  // open: dp
endmodule
