// Logisim project full adder.circ as structural Verilog
module main (
  input  in_1,
  input  in_2
);

  wire half_adder_1_out_3, half_adder_1_out_4;

  half_adder half_adder_1 (.A(in_1), .B(in_2), .out_3(half_adder_1_out_3), .out_4(half_adder_1_out_4));
  LED Sum (.in(half_adder_1_out_3));
  LED Carry (.in(half_adder_1_out_4));
endmodule

module half_adder (
  input  A,
  input  B,
  output out_3,
  output out_4
);

  wire A_prime_B_out, AB_prime_out, not_1_out, not_2_out;

  not not_1 (not_1_out, A);
  not not_2 (not_2_out, B);
  and A_prime_B (A_prime_B_out, not_1_out, B);
  and AB_prime (AB_prime_out, A, not_2_out);
  and and_1 (out_4, A, B);
  or A_prime_B_AB_prime (out_3, A_prime_B_out, AB_prime_out);
endmodule

module Full_adder (
  input  A,
  input  B,
  input  C
);

  wire xor_1_out;

  ExactlyOne xor_1 (.out(xor_1_out), .in0(A), .in1(B), .in2(C));
  // AND_Gate and_1 is placed but not wired
endmodule
