// Logisim project ram.circ as structural Verilog: 5 circuits, main circuit main
module main (
  input  [7:0] Addr,
  input  [7:0] Data_in,
  input  R_W_prime,
  output [7:0] data_out
);

  wire clock_1_out, not_1_out;

  not not_1 (not_1_out, R_W_prime);
  Clock clock_1 (.out(clock_1_out));
  RAM #(.bus("separate")) ram_1 (
    .addr(Addr), .din(Data_in), .data(data_out), .str(R_W_prime), .clk(clock_1_out), .ld(not_1_out));  // open: sel, clr
endmodule

module ram2 (
  input  [8:0] in_1,
  input  [3:0] in_2,
  input  in_3,
  output [3:0] out_4
);

  wire clock_1_out, not_1_out;

  not not_1 (not_1_out, in_3);
  Clock clock_1 (.out(clock_1_out));
  RAM #(.addrWidth(9), .dataWidth(4), .bus("separate")) ram_1 (
    .addr(in_1), .din(in_2), .data(out_4), .str(not_1_out), .clk(clock_1_out), .ld(in_3));  // open: sel, clr
endmodule

module _256x16_by_256x8 (
  input  [15:0] in_1,
  input  [7:0] in_2,
  input  in_3,
  output [7:0] out_4,
  output [7:0] out_5
);

  wire clock_1_out, not_1_out;

  Clock clock_1 (.out(clock_1_out));
  not not_1 (not_1_out, in_3);
  RAM #(.bus("separate")) ram_1 (
    .addr(in_2), .din(in_1[15:8]), .data(out_4), .str(not_1_out), .clk(clock_1_out), .ld(in_3));  // open: sel, clr
  RAM #(.bus("separate")) ram_2 (
    .addr(in_2), .din(in_1[7:0]), .data(out_5), .str(not_1_out), .clk(clock_1_out), .ld(in_3));  // open: sel, clr
endmodule

module _512_x_16_using_256x8 (
  input  [8:0] in_1,
  input  [15:0] in_2,
  input  in_3,
  output [7:0] out_4,
  output [7:0] out_5
);

  wire clock_1_out, decoder_1_out0, decoder_1_out1, not_1_out;

  Decoder #(.enable("false")) decoder_1 (.out0(decoder_1_out0), .out1(decoder_1_out1), .sel(in_1[8]));
  not not_1 (not_1_out, in_3);
  Clock clock_1 (.out(clock_1_out));
  RAM #(.bus("separate")) ram_1 (
    .addr(in_1[7:0]), .din(in_2[15:8]), .data(out_4), .str(not_1_out), .sel(decoder_1_out0),
    .clk(clock_1_out), .ld(in_3));  // open: clr
  RAM #(.bus("separate")) ram_2 (
    .addr(in_1[7:0]), .din(in_2[15:8]), .data(out_4), .str(not_1_out), .sel(decoder_1_out1),
    .clk(clock_1_out), .ld(in_3));  // open: clr
  RAM #(.bus("separate")) ram_3 (
    .addr(in_1[7:0]), .din(in_2[7:0]), .data(out_5), .str(not_1_out), .sel(decoder_1_out0),
    .clk(clock_1_out), .ld(in_3));  // open: clr
  RAM #(.bus("separate")) ram_4 (
    .addr(in_1[7:0]), .din(in_2[7:0]), .data(out_5), .str(not_1_out), .sel(decoder_1_out1),
    .clk(clock_1_out), .ld(in_3));  // open: clr
endmodule

module _256x16_using_64x8 (
  input  [7:0] in_1,
  input  [15:0] in_2,
  input  in_3,
  output [7:0] out_4,
  output [7:0] out_5
);

  wire clock_1_out, decoder_1_out0, decoder_1_out1, decoder_1_out2, decoder_1_out3, not_1_out;

  Decoder #(.select(2), .enable("false")) decoder_1 (
    .out0(decoder_1_out0), .out1(decoder_1_out1), .out2(decoder_1_out2), .out3(decoder_1_out3),
    .sel(in_1[7:6]));
  RAM #(.addrWidth(6), .bus("separate")) ram_1 (
    .addr(in_1[5:0]), .din(in_2[15:8]), .data(out_5), .str(not_1_out), .sel(decoder_1_out0),
    .clk(clock_1_out), .ld(in_3));  // open: clr
  RAM #(.addrWidth(6), .bus("separate")) ram_2 (
    .addr(in_1[5:0]), .din(in_2[15:8]), .data(out_5), .str(not_1_out), .sel(decoder_1_out1),
    .clk(clock_1_out), .ld(in_3));  // open: clr
  RAM #(.addrWidth(6), .bus("separate")) ram_3 (
    .addr(in_1[5:0]), .din(in_2[15:8]), .data(out_5), .str(not_1_out), .sel(decoder_1_out2),
    .clk(clock_1_out), .ld(in_3));  // open: clr
  RAM #(.addrWidth(6), .bus("separate")) ram_4 (
    .addr(in_1[5:0]), .din(in_2[15:8]), .data(out_5), .str(not_1_out), .sel(decoder_1_out3),
    .clk(clock_1_out), .ld(in_3));  // open: clr
  not not_1 (not_1_out, in_3);
  Clock clock_1 (.out(clock_1_out));
  RAM #(.addrWidth(6), .bus("separate")) ram_5 (
    .addr(in_1[5:0]), .din(in_2[7:0]), .data(out_4), .str(not_1_out), .sel(decoder_1_out0),
    .clk(clock_1_out), .ld(in_3));  // open: clr
  RAM #(.addrWidth(6), .bus("separate")) ram_6 (
    .addr(in_1[5:0]), .din(in_2[7:0]), .data(out_4), .str(not_1_out), .sel(decoder_1_out1),
    .clk(clock_1_out), .ld(in_3));  // open: clr
  RAM #(.addrWidth(6), .bus("separate")) ram_7 (
    .addr(in_1[5:0]), .din(in_2[7:0]), .data(out_4), .str(not_1_out), .sel(decoder_1_out2),
    .clk(clock_1_out), .ld(in_3));  // open: clr
  RAM #(.addrWidth(6), .bus("separate")) ram_8 (
    .addr(in_1[5:0]), .din(in_2[7:0]), .data(out_4), .str(not_1_out), .sel(decoder_1_out3),
    .clk(clock_1_out), .ld(in_3));  // open: clr
endmodule
